// Digital circuit A.dig as structural Verilog
module A (
  input  [7:0] IN,
  input  [3:0] CON,
  input  C_in,
  input  SI,
  output [3:0] AL,
  output [3:0] AH,
  output SO
);

  wire [3:0] _74195_p8;
  wire [3:1] _74195_p6;

  // _74194 _74195: pin names not known; wires that end beside it: CON[1], CON[3], CON[2], CON[0], C_in, _74195_p6[3], IN[7], _74195_p8[3], IN[6], _74195_p8[2], IN[5], _74195_p8[1], IN[4], _74195_p8[0], CON[1], CON[3], CON[2]
  assign AH = ~_74195_p8;  // Not not_1, 4 bits wide
  // _74194 _74195_2: pin names not known; wires that end beside it: CON[0], _74195_p8[0], SI, IN[3], _74195_p6[3], IN[2], _74195_p6[2], IN[1], _74195_p6[1], IN[0], SO
  assign AL = ~{_74195_p6, SO};  // Not not_2, 4 bits wide

  // Other names for the same wires on the sheet: ACP = CON[0]; nAMR = CON[1]; S0 = CON[2]; S1 = CON[3]
endmodule
