// Digital circuit ALU beta.dig as structural Verilog
module ALU_beta (
  input  clk,
  output [7:0] B,
  output [7:0] A,
  output Co,
  output [7:0] BD
);

  wire _74138_2_p12, _74138_2_p13, _74138_4_p14, _74141_p7, _74141_p8, _74141_p9, _74141_p10, _74141_p11,
       _74161_1_p14, _74165_1_p14, _74165_1_p15, _74174_1_p9, _74174_1_p10, _74174_1_p11, _74273_1_p10,
       _74273_2_p16, BHLD, BLLD, BRK, C_half, CIN, CKI, CLD, D, d_ff_as_2_q, DCK, JMP, LCP, M,
       M_register_p13, M_register_p14, M_register_p15, M_register_p16, MCK, MOU, nACO, nACP, nAILD,
       nand_1_out, nAOO, nBUSO, nCAI, nCLC, nDO, nLD, nMLD, nNF, not_8_out, not_11_out, nREC, nSEO, nSTC,
       nSTL, nSTR, nUO, O0, or_1_out, OV, P0, P1, P2, reset_2_out, reset_3_out, rs_ff_as_1_q, SFK, SI, SO, Z;
  wire [2:0] O, rom_1_d_3;
  wire [3:0] _74181_2_p19, _74181_p16, _74273_1_p14, _74273_1_p18, CON, nAH, nAL, nBH, nBL, S;
  wire [4:0] P, rom_1_d_2;
  wire [7:0] _74161_2_p13, BH_Register_p18, BUS_in, not_12_out, rom_1_d;

  // _74273 _74273_1: pin names not known; wires that end beside it: BD[0], BD[1], BD[2], BD[3], BD[4], BD[5], BD[6], BD[7], LCP, _74273_1_p10, _74273_1_p14[0], _74273_1_p14[1], _74273_1_p14[2], _74273_1_p14[3], _74273_1_p18[0], _74273_1_p18[1], _74273_1_p18[2], _74273_1_p18[3]
  Reset reset_1 (.out(_74273_1_p10));
  or or_1 (or_1_out, reset_2_out, CKI);
  Reset #(.invertOutput("false")) reset_2 (.out(reset_2_out));
  nand nand_1 (nand_1_out, ~clk, JMP);  // NAnd
  RS_FF_AS rs_ff_as_1 (.S(or_1_out), .R(BRK), .Q(rs_ff_as_1_q));  // open: nQ
  Reset reset_3 (.out(reset_3_out));
  // _74161 _74161_1: pin names not known; wires that end beside it: _74273_1_p14[0], _74273_1_p14[1], _74273_1_p14[2], _74273_1_p14[3], nand_1_out, reset_3_out, clk, rs_ff_as_1_q, rs_ff_as_1_q, _74161_2_p13[0], _74161_2_p13[1], _74161_2_p13[2], _74161_2_p13[3], _74161_1_p14
  // _74161 _74161_2: pin names not known; wires that end beside it: _74273_1_p18[0], _74273_1_p18[1], _74273_1_p18[2], _74273_1_p18[3], nand_1_out, reset_3_out, clk, _74161_1_p14, _74161_1_p14, _74161_2_p13[4], _74161_2_p13[5], _74161_2_p13[6], _74161_2_p13[7]
  // Probe on _74161_2_p13
  ROM #(.AddrBits(8), .Bits(16)) rom_1 (.A(_74161_2_p13), .sel(1'b1), .D({rom_1_d_3, rom_1_d_2, rom_1_d}));
  Seven_Seg_Hex seven_seg_hex_1 (.d(BD[7:4]), .dp(1'b0));
  Seven_Seg_Hex seven_seg_hex_2 (.d(BD[3:0]), .dp(1'b0));
  D_FF #(.Bits(8)) d_ff_1 (.D(rom_1_d), .C(~clk), .Q(BUS_in));  // open: nQ
  D_FF #(.Bits(5)) d_ff_2 (.D(rom_1_d_2), .C(~clk), .Q(P));  // open: nQ
  D_FF #(.Bits(3)) d_ff_3 (.D(rom_1_d_3), .C(~clk), .Q(O));  // open: nQ
  // Probe on BUS_in
  // Probe on P
  // Probe on O
  // _74138 _74141: pin names not known; wires that end beside it: P[0], P[1], P[2], 1'b1, 1'b0, P2, _74141_p7, _74141_p8, _74141_p9, _74141_p10, _74141_p11
  // _74138 _74138: pin names not known; wires that end beside it: P[3], P[4], 1'b0, 1'b1, 1'b0, 1'b0, P0, P1, P2
  // _74174 _74174_1: pin names not known; wires that end beside it: O[0], O[1], O[2], 1'b0, 1'b0, 1'b0, nSEO, 1'b1, _74174_1_p9, _74174_1_p10, _74174_1_p11
  not not_1 (CKI, _74141_p7);
  not not_2 (BRK, _74141_p8);
  not not_3 (JMP, _74141_p9);
  not not_4 (LCP, _74141_p10);
  not not_5 (nSEO, _74141_p11);
  // Probe on {nAH, nAL}
  // Probe on {nBH, nBL}
  // _74244 _74244_1: pin names not known; wires that end beside it: BUS_in[0], BUS_in[1], BUS_in[2], BUS_in[3], BUS_in[4], BUS_in[5], BUS_in[6], BUS_in[7], nBUSO, nBUSO, BD[0], BD[1], BD[2], BD[3], BD[4], BD[5], BD[6], BD[7]
  // _74138 _74140: pin names not known; wires that end beside it: _74174_1_p9, _74174_1_p10, _74174_1_p11, 1'b1, 1'b0, 1'b0, O0
  // _74165 M_register: pin names not known; wires that end beside it: BD[7], BD[6], BD[5], BD[4], BD[3], BD[2], BD[1], BD[0], 1'b0, 1'b0, MCK, nMLD, M_register_p13, M_register_p14, M_register_p15, M_register_p16
  // _74273 _74273_2: pin names not known; wires that end beside it: BD[0], BD[1], BD[2], BD[3], BD[4], BD[5], BD[6], BD[7], CLD, 1'b1, S[0], S[1], S[2], S[3], MOU, _74273_2_p16, M, D
  // _74138 _74138_2: pin names not known; wires that end beside it: P[0], P[1], P[2], clk, 1'b0, P0, nACP, CON[1], nSTL, nSTR, nLD, _74138_2_p12, _74138_2_p13
  // _74138 _74138_3: pin names not known; wires that end beside it: O[0], O[1], O[2], 1'b1, 1'b0, O0, nUO, nDO, nAOO, nACO, nBUSO
  not not_6 (BLLD, _74138_2_p12);
  not not_7 (BHLD, _74138_2_p13);
  // Probe on M_register_p15
  // Probe on M_register_p16
  LED led_1 (.in(_74273_2_p16));
  // _74574 BH_Register: pin names not known; wires that end beside it: BD[0], BD[1], BD[2], BD[3], BD[4], BD[5], BD[6], BD[7], M_register_p14, BHLD, BH_Register_p18[0], BH_Register_p18[1], BH_Register_p18[2], BH_Register_p18[3], BH_Register_p18[4], BH_Register_p18[5], BH_Register_p18[6], BH_Register_p18[7]
  D_FF_AS d_ff_as_1 (.Set(~nSTC), .D(Co), .C(~nREC), .Clr(~nCLC), .Q(CIN));  // open: nQ
  // _74138 _74138_4: pin names not known; wires that end beside it: P[0], P[1], P[2], clk, 1'b0, P1, nAILD, nMLD, nSTC, nCLC, nREC, nNF, nCAI, _74138_4_p14
  not not_8 (not_8_out, nAOO);
  // _74541 _74541: pin names not known; wires that end beside it: S[0], S[1], S[2], S[3], MOU, CIN, Z, OV, nACO, nACO, BD[0], BD[1], BD[2], BD[3], BD[4], BD[5], BD[6], BD[7]
  // _74595 _74595_1: pin names not known; wires that end beside it: SO, not_8_out, 1'b1, SFK, nAOO, BD[7], BD[6], BD[5], BD[4], BD[3], BD[2], BD[1], BD[0]
  // _74574 BL_Register: pin names not known; wires that end beside it: BD[0], BD[1], BD[2], BD[3], BD[4], BD[5], BD[6], BD[7], M_register_p13, BLLD, BH_Register_p18[0], BH_Register_p18[1], BH_Register_p18[2], BH_Register_p18[3], BH_Register_p18[4], BH_Register_p18[5], BH_Register_p18[6], BH_Register_p18[7]
  assign {nBH, nBL} = ~BH_Register_p18;  // Not not_9, 8 bits wide
  not not_10 (CLD, _74138_4_p14);
  // ACON acon_1: pin names not known; wires that end beside it: M, D, nLD, nSTR, nSTL, nACP, Co, nNF, clk, CON[0], SFK, CON[2], CON[3], MCK, DCK
  D_FF_AS d_ff_as_2 (.Set(~1'b1), .D(Co), .C(SFK), .Clr(~nCAI), .Q(d_ff_as_2_q));  // open: nQ
  not not_11 (not_11_out, nDO);
  // _74165 _74165_1: pin names not known; wires that end beside it: BD[0], BD[1], BD[2], BD[3], BD[4], BD[5], BD[6], BD[7], 1'b0, 1'b0, SFK, nAILD, SI, _74165_1_p14, _74165_1_p15
  A a_1 (.IN(BD), .CON(CON), .C_in(d_ff_as_2_q), .SI(SI), .AL(nAL), .AH(nAH), .SO(SO));
  // _74595 _74595_2: pin names not known; wires that end beside it: Co, not_11_out, 1'b1, DCK, nDO, BD[0], BD[1], BD[2], BD[3], BD[4], BD[5], BD[6], BD[7]
  // Probe on _74165_1_p14
  // Probe on _74165_1_p15
  // _74181 _74181: pin names not known; wires that end beside it: nAL[0], nAL[1], nAL[2], nAL[3], nBL[0], nBL[1], nBL[2], nBL[3], S[0], S[1], S[2], S[3], _74181_p16[0], _74181_p16[1], _74181_p16[2], _74181_p16[3]
  // _74181 _74181_2: pin names not known; wires that end beside it: MOU, CIN, nAH[0], nAH[1], nAH[2], nAH[3], nBH[0], nBH[1], nBH[2], nBH[3], S[0], S[1], S[2], S[3], MOU, C_half, Z, C_half, _74181_2_p19[0], _74181_2_p19[1], _74181_2_p19[2], _74181_2_p19[3], Z, Co
  assign not_12_out = ~{_74181_2_p19, _74181_p16};  // Not not_12, 8 bits wide
  // Probe on not_12_out
  PullUp pullup_1 (.out(Z));
  // _74540 _74540_1: pin names not known; wires that end beside it: _74181_p16[0], _74181_p16[1], _74181_p16[2], _74181_p16[3], _74181_2_p19[0], _74181_2_p19[1], _74181_2_p19[2], _74181_2_p19[3], nUO, nUO, BD[0], BD[1], BD[2], BD[3], BD[4], BD[5], BD[6], BD[7]
  OV ov_1 (.nAH(nAH[3]), .nBH(nBH[3]), .nF3(_74181_2_p19[3]), .OV(OV));
  assign A = ~{nAH, nAL};  // Not not_13, 8 bits wide
  assign B = ~{nBH, nBL};  // Not not_14, 8 bits wide

  // Other names for the same wires on the sheet: BUS[7:0] = BD; nAMR = CON[1]

  // Notes on the sheet:
  //   clk: Hz: 3
  //   contents of rom_1 (hex, n*v repeats v):
  //   0,8200,8851,8000,8900,8000,8620,8a00,8f46,300,100,100,100,100,100,100,100,100,100,
  //   100,100,100,100,100,100,100,2000,3300,0,8600,1300,0,8200,8600,87ff,89ff,8400,8fc9,
  //   8b00,8e00,d00,100,100,100,100,100,100,100,100,100,100,100,100,100,100,100,100,100,
  //   4e00,5300,8600,1300
  //   created by Left Hand... 
  //   An open sourse mirco computer
endmodule
