// Digital circuit ALU beta.dig as structural Verilog
module ALU_beta (
  input  [7:0] BUS,
  input  [2:0] P,
  input  [2:0] PS,
  input  [2:0] O,
  input  [2:0] OS,
  input  CLK,
  output [7:0] A,
  output [7:0] B,
  output [7:0] F
);

  wire _74138_3_p14, _74138_p12, _74138_p13, _74142_p4, _74165_1_p14, _74165_1_p15, _74273_1_p16,
       _74595_1_p2, _74595_1_p14, _74595_2_p2, _74595_2_p15, BHLD, BLLD, C_half, Ci, CLD, Co, d_ff_as_2_q,
       DCK, DIV, M, M_register_p13, M_register_p14, M_register_p15, M_register_p16, MCK, MUL, nACO, nACP,
       nAILD, nAOO, nCAI, nCLC, nDO, nLDM, nMLD, nNF, nREC, nSTC, nSTL, nSTR, nUO, OV, PG0, PG1, SFK, SI, SO,
       Z;
  wire [3:0] _74181_2_p18, _74181_p16, CON, nAH, nAL, nBH, nBL, S;
  wire [7:0] BH_Register_p18;

  // _74165 M_register: pin names not known; wires that end beside it: BUS[7], BUS[6], BUS[5], BUS[4], BUS[3], BUS[2], BUS[1], BUS[0], 1'b0, 1'b0, MCK, nMLD, M_register_p13, M_register_p14, M_register_p15, M_register_p16
  // _74273 _74273_1: pin names not known; wires that end beside it: BUS[0], BUS[1], BUS[2], BUS[3], BUS[4], BUS[5], BUS[6], BUS[7], CLD, 1'b1, S[0], S[1], S[2], S[3], M, _74273_1_p16, MUL, DIV
  // _74138 _74138: pin names not known; wires that end beside it: P[0], P[1], P[2], CLK, 1'b0, PG0, nACP, CON[1], nSTL, nSTR, nLDM, _74138_p12, _74138_p13
  // _74138 _74138_2: pin names not known; wires that end beside it: PS[0], PS[1], PS[2], 1'b1, 1'b0, 1'b0, PG0, PG1
  not not_1 (BLLD, _74138_p12);
  not not_2 (BHLD, _74138_p13);
  // Probe on M_register_p15
  // Probe on M_register_p16
  LED led_1 (.in(_74273_1_p16));
  // _74574 BH_Register: pin names not known; wires that end beside it: BUS[0], BUS[1], BUS[2], BUS[3], BUS[4], BUS[5], BUS[6], BUS[7], M_register_p14, BHLD, BH_Register_p18[0], BH_Register_p18[1], BH_Register_p18[2], BH_Register_p18[3], BH_Register_p18[4], BH_Register_p18[5], BH_Register_p18[6], BH_Register_p18[7]
  D_FF_AS d_ff_as_1 (.Set(~nSTC), .D(Co), .C(~nREC), .Clr(~nCLC), .Q(Ci));  // open: nQ
  // _74138 _74138_3: pin names not known; wires that end beside it: P[0], P[1], P[2], CLK, 1'b0, PG1, nAILD, nMLD, nSTC, nCLC, nREC, nNF, nCAI, _74138_3_p14
  // _74138 _74142: pin names not known; wires that end beside it: O[0], O[1], O[2], _74142_p4, OS[1], OS[2], nUO, nDO, nAOO, nACO
  not not_3 (_74142_p4, OS[0]);
  // _74541 _74541: pin names not known; wires that end beside it: S[0], S[1], S[2], S[3], M, Co, Z, OV, nACO, nACO, BUS[0], BUS[1], BUS[2], BUS[3], BUS[4], BUS[5], BUS[6], BUS[7]
  // _74574 BL_Register: pin names not known; wires that end beside it: BUS[0], BUS[1], BUS[2], BUS[3], BUS[4], BUS[5], BUS[6], BUS[7], M_register_p13, BLLD, BH_Register_p18[0], BH_Register_p18[1], BH_Register_p18[2], BH_Register_p18[3], BH_Register_p18[4], BH_Register_p18[5], BH_Register_p18[6], BH_Register_p18[7]
  assign {nBH, nBL} = ~BH_Register_p18;  // Not not_4, 8 bits wide
  not not_5 (CLD, _74138_3_p14);
  // ACON acon_1: pin names not known; wires that end beside it: MUL, DIV, nLDM, nSTR, nSTL, nACP, Co, nNF, CLK, CON[0], CON[2], CON[3], SFK, MCK, DCK
  D_FF_AS d_ff_as_2 (.Set(~1'b1), .D(Co), .C(SFK), .Clr(~nCAI), .Q(d_ff_as_2_q));  // open: nQ
  // _74595 _74595_1: pin names not known; wires that end beside it: SO, _74595_1_p2, 1'b1, SFK, nAOO, BUS[7], BUS[6], BUS[5], BUS[4], BUS[3], BUS[2], BUS[1], BUS[0], _74595_1_p14
  not not_6 (_74595_1_p2, nAOO);
  // _74165 _74165_1: pin names not known; wires that end beside it: BUS[0], BUS[1], BUS[2], BUS[3], BUS[4], BUS[5], BUS[6], BUS[7], 1'b0, 1'b0, SFK, nAILD, SI, _74165_1_p14, _74165_1_p15
  A a_1 (.IN(BUS), .CON(CON), .C_in(d_ff_as_2_q), .SI(SI), .AL(nAL), .AH(nAH), .SO(SO));
  // Probe on _74595_1_p14
  // Probe on _74165_1_p14
  // Probe on _74165_1_p15
  // _74595 _74595_2: pin names not known; wires that end beside it: Co, _74595_2_p2, 1'b1, DCK, nDO, C_half, BUS[0], BUS[1], BUS[2], BUS[3], BUS[4], BUS[5], BUS[6], BUS[7], _74595_2_p15, Co
  not not_7 (_74595_2_p2, nDO);
  // _74181 _74181: pin names not known; wires that end beside it: nAL[0], nAL[1], nAL[2], nAL[3], nBL[0], nBL[1], nBL[2], nBL[3], S[0], S[1], S[2], S[3], _74181_p16[0], _74181_p16[1], _74181_p16[2], _74181_p16[3]
  // _74181 _74181_2: pin names not known; wires that end beside it: M, Ci, nAH[0], nAH[1], nAH[2], nAH[3], nBH[0], nBH[1], nBH[2], nBH[3], S[0], S[1], S[2], S[3], M, Z, C_half, _74181_2_p18[0], _74181_2_p18[1], _74181_2_p18[2], _74181_2_p18[3], Z
  // Probe on _74595_2_p15
  assign F = ~{_74181_2_p18, _74181_p16};  // Not not_8, 8 bits wide
  PullUp pullup_1 (.out(Z));
  // _74540 _74540_1: pin names not known; wires that end beside it: _74181_p16[0], _74181_p16[1], _74181_p16[2], _74181_p16[3], _74181_2_p18[0], _74181_2_p18[1], _74181_2_p18[2], _74181_2_p18[3], nUO, nUO, BUS[0], BUS[1], BUS[2], BUS[3], BUS[4], BUS[5], BUS[6], BUS[7], BUS
  OV ov_1 (.nAH(nAH[3]), .nBH(nBH[3]), .nF3(_74181_2_p18[3]), .OV(OV));
  assign A = ~{nAH, nAL};  // Not not_9, 8 bits wide
  assign B = ~{nBH, nBL};  // Not not_10, 8 bits wide

  // Other names for the same wires on the sheet: nAMR = CON[1]

  // Notes on the sheet:
  //   created by Left Hand... 
  //   An open sourse 
  //   mirco computer
endmodule
