// Digital circuit #ACON.dig as structural Verilog
module ACON (
  input  M,
  input  D,
  input  nLDM,
  input  nSTR,
  input  nSTL,
  input  nACP,
  input  Cin,
  input  nNF,
  input  C,
  output ACP,
  output SFK,
  output S0,
  output S1,
  output MCK,
  output DCK
);

  wire and_1_out, b, c_t, d_ff_as_1_q, d_ff_as_2_q, d_ff_as_3_q, f, h, nand_1_out, nand_6_out, nor_1_out,
       nor_2_out, nor_3_out, not_1_out, not_3_out;

  not not_1 (not_1_out, nACP);
  nand nand_1 (nand_1_out, nSTL, nSTR);
  nor nor_1 (nor_1_out, D, DCK, Cin);
  not not_2 (b, nand_1_out);
  not not_3 (not_3_out, SFK);
  D_FF_AS d_ff_as_1 (.Set(~1'b1), .D(DCK), .C(not_1_out), .Clr(~M), .Q(d_ff_as_1_q), .nQ(DCK));
  D_FF_AS d_ff_as_2 (.Set(~1'b1), .D(nor_1_out), .C(C), .Clr(~1'b1), .Q(d_ff_as_2_q));  // open: nQ
  D_FF_AS d_ff_as_3 (.Set(~1'b1), .D(1'b1), .C(not_3_out), .Clr(~nNF), .Q(d_ff_as_3_q));  // open: nQ
  nor nor_2 (nor_2_out, f, d_ff_as_1_q, c_t);
  nor nor_3 (nor_3_out, h, d_ff_as_1_q, c_t);
  nor nor_4 (ACP, d_ff_as_2_q, nACP);
  nand nand_2 (SFK, DCK, nACP);
  and and_1 (and_1_out, SFK, d_ff_as_3_q);
  nand nand_3 (f, nSTR, h);
  nand nand_4 (h, f, nSTL);
  nand nand_5 (c_t, nLDM, nand_6_out);
  nand nand_6 (nand_6_out, c_t, b);
  not not_4 (S0, nor_2_out);
  not not_5 (S1, nor_3_out);
  not not_6 (MCK, and_1_out);

  // Other names for the same wires on the sheet: a = nLDM; e = nSTR; g = nSTL

  // Notes on the sheet:
  //   M: default 1
  //   D: default 1
  //   nLDM: default 1
  //   nSTR: default 1
  //   nSTL: default 1
  //   nACP: default 1
  //   nNF: default 1
  //   C: default 1
endmodule
