// Digital circuit ACON.dig as structural Verilog
module ACON (
  input  M,
  input  D,
  input  nLDM,
  input  nSTR,
  input  nSTL,
  input  nACP,
  input  Cin,
  input  nNF,
  input  CLK,
  output ACP,
  output S0,
  output S1,
  output SFK,
  output MCK,
  output DCK
);

  wire and_1_out, d_ff_as_1_q, d_ff_as_2_q, d_ff_as_3_q, nor_1_out, rs_ff_as_1_q, rs_ff_as_2_nq, rs_ff_as_2_q;

  and and_1 (and_1_out, nSTL, nSTR);
  nor nor_1 (nor_1_out, D, DCK, Cin);
  RS_FF_AS rs_ff_as_1 (.S(~nLDM), .R(~and_1_out), .Q(rs_ff_as_1_q));  // open: nQ
  RS_FF_AS rs_ff_as_2 (.S(~nSTR), .R(~nSTL), .Q(rs_ff_as_2_q), .nQ(rs_ff_as_2_nq));
  D_FF_AS d_ff_as_1 (.Set(~1'b1), .D(DCK), .C(~nACP), .Clr(~M), .Q(d_ff_as_1_q), .nQ(DCK));
  D_FF_AS d_ff_as_2 (.Set(~1'b1), .D(nor_1_out), .C(CLK), .Clr(~1'b1), .Q(d_ff_as_2_q));  // open: nQ
  D_FF_AS d_ff_as_3 (.Set(~1'b1), .D(1'b1), .C(~SFK), .Clr(~nNF), .Q(d_ff_as_3_q));  // open: nQ
  or or_1 (S0, rs_ff_as_2_q, d_ff_as_1_q, rs_ff_as_1_q);
  or or_2 (S1, rs_ff_as_2_nq, d_ff_as_1_q, rs_ff_as_1_q);
  nor nor_2 (ACP, d_ff_as_2_q, nACP);
  nand nand_1 (SFK, DCK, nACP);
  nand nand_2 (MCK, SFK, d_ff_as_3_q);

  // Notes on the sheet:
  //   M: default 1
  //   D: default 1
  //   nLDM: default 1
  //   nSTR: default 1
  //   nSTL: default 1
  //   nACP: default 1
  //   nNF: default 1
  //   CLK: default 1
endmodule
