// Digital circuit ALU.dig as structural Verilog
module ALU (
  input  [7:0] A,
  input  [7:0] B,
  input  [5:0] S,
  input  O,
  output [7:0] BUS,
  output [5:0] PSW
);

  wire [2:0] _74181_2_p19;
  wire [3:1] _74181_p16;

  // _74181 _74181: pin names not known; wires that end beside it: A[0], A[1], A[2], A[3], B[0], B[1], B[2], B[3], S[0], S[1], S[2], S[3], PSW[0], _74181_p16[1], _74181_p16[2], _74181_p16[3]
  // _74181 _74181_2: pin names not known; wires that end beside it: S[4], S[5], A[4], A[5], A[6], A[7], B[4], B[5], B[6], B[7], S[0], S[1], S[2], S[3], S[4], PSW[1], PSW[4], PSW[1], _74181_2_p19[0], _74181_2_p19[1], _74181_2_p19[2], PSW[3], PSW[4], PSW[5]
  PullUp pullup_1 (.out(PSW[4]));
  // _74540 _74540_1: pin names not known; wires that end beside it: PSW[0], _74181_p16[1], _74181_p16[2], _74181_p16[3], _74181_2_p19[0], _74181_2_p19[1], _74181_2_p19[2], PSW[3], O, O, BUS[0], BUS[1], BUS[2], BUS[3], BUS[4], BUS[5], BUS[6], BUS[7]
  OV ov_1 (.nAH(A[7]), .nBH(B[7]), .nF3(PSW[3]), .OV(PSW[2]));

  // Other names for the same wires on the sheet: nAH = A[7]; nBH = B[7]; C_H = PSW[1]; OE = O

  // Notes on the sheet:
  //   fault low
  //   carry half
  //   fault high
  //   zero
  //   carry output
  //   overflow
endmodule
