// Digital circuit OV.dig as structural Verilog
module OV (
  input  nAH,
  input  nBH,
  input  nF3,
  output OV
);

  wire nand_1_out, nand_2_out;

  nand nand_1 (nand_1_out, nAH, nBH, ~nF3);  // NAnd
  nand nand_2 (nand_2_out, ~nAH, ~nBH, nF3);  // NAnd
  nand nand_3 (OV, nand_1_out, 1'b1, nand_2_out);
endmodule
