// Digital circuit old alu.dig as structural Verilog
module old_alu (
  input  [7:0] BUS,
  input  [5:0] P,
  input  [5:0] O,
  input  C,
  output [7:0] B,
  output [7:0] A,
  output Co,
  output [7:0] BD
);

  wire _74138_2_p12, _74138_2_p13, _74139_p4, _74273_1_p16, _74595_2_p2, BHLD, BLLD, C_half, CIN, CLD, D,
       d_ff_as_2_q, DCK, M, M_register_p13, M_register_p14, MCK, MOU, nACO, nACP, nAILD, nAMR, nAOO, nBUSO,
       nCAI, nCLC, nDO, nLD, nMLD, nNF, not_5_out, nREC, nSTC, nSTL, nSTR, nUO, OV, P0, P1, SFK, SI, SO, Z;
  wire [3:0] _74181_2_p19, _74181_p16, acon_1_p10, nAH, nAL, nBH, nBL, S;
  wire [7:0] BH_Register_p18, not_7_out;

  // _74244 _74244_1: pin names not known; wires that end beside it: BUS[0], BUS[1], BUS[2], BUS[3], BUS[4], BUS[5], BUS[6], BUS[7], nBUSO, nBUSO, BD[0], BD[1], BD[2], BD[3], BD[4], BD[5], BD[6], BD[7]
  // _74165 M_register: pin names not known; wires that end beside it: BD[7], BD[6], BD[5], BD[4], BD[3], BD[2], BD[1], BD[0], 1'b0, 1'b0, MCK, nMLD, M_register_p13, M_register_p14
  // _74273 _74273_1: pin names not known; wires that end beside it: BD[0], BD[1], BD[2], BD[3], BD[4], BD[5], BD[6], BD[7], CLD, 1'b1, S[0], S[1], S[2], S[3], MOU, _74273_1_p16, M, D
  // _74138 _74138: pin names not known; wires that end beside it: P[3], P[4], P[5], C, 1'b0, 1'b0, P0, P1
  // _74138 _74139: pin names not known; wires that end beside it: O[0], O[1], O[2], _74139_p4, O[4], O[5], nUO, nDO, nAOO, nACO, nBUSO
  not not_1 (_74139_p4, O[3]);
  // _74574 BH_Register: pin names not known; wires that end beside it: BD[0], BD[1], BD[2], BD[3], BD[4], BD[5], BD[6], BD[7], M_register_p14, BHLD, BH_Register_p18[0], BH_Register_p18[1], BH_Register_p18[2], BH_Register_p18[3], BH_Register_p18[4], BH_Register_p18[5], BH_Register_p18[6], BH_Register_p18[7]
  LED led_1 (.in(_74273_1_p16));
  D_FF_AS d_ff_as_1 (.Set(~nSTC), .D(Co), .C(~nREC), .Clr(~nCLC), .Q(CIN));  // open: nQ
  // _74138 _74138_2: pin names not known; wires that end beside it: P[0], P[1], P[2], 1'b1, 1'b0, P0, nACP, nAMR, nSTL, nSTR, nLD, _74138_2_p12, _74138_2_p13
  // _74541 _74541: pin names not known; wires that end beside it: S[0], S[1], S[2], S[3], CIN, Z, OV, C_half, nACO, nACO, BD[0], BD[1], BD[2], BD[3], BD[4], BD[5], BD[6], BD[7]
  not not_2 (BLLD, _74138_2_p12);
  not not_3 (BHLD, _74138_2_p13);
  // _74574 BL_Register: pin names not known; wires that end beside it: BD[0], BD[1], BD[2], BD[3], BD[4], BD[5], BD[6], BD[7], M_register_p13, BLLD, BH_Register_p18[0], BH_Register_p18[1], BH_Register_p18[2], BH_Register_p18[3], BH_Register_p18[4], BH_Register_p18[5], BH_Register_p18[6], BH_Register_p18[7]
  assign {nBH, nBL} = ~BH_Register_p18;  // Not not_4, 8 bits wide
  not not_5 (not_5_out, nAOO);
  // _74595 _74595_1: pin names not known; wires that end beside it: BD[0], BD[1], BD[2], BD[3], BD[4], BD[5], BD[6], BD[7], nAOO, SFK, 1'b1, not_5_out, SO
  // _74138 _74138_3: pin names not known; wires that end beside it: P[0], P[1], P[2], 1'b1, 1'b0, P1, nAILD, nMLD, nSTC, nCLC, nREC, nNF, nCAI, CLD, C
  // ACON acon_1: pin names not known; wires that end beside it: M, D, nLD, nSTR, nSTL, nACP, Co, nNF, C, acon_1_p10[0], acon_1_p10[2], acon_1_p10[3], SFK, MCK, DCK
  // _74165 _74165_1: pin names not known; wires that end beside it: BD[0], BD[1], BD[2], BD[3], BD[4], BD[5], BD[6], BD[7], 1'b0, 1'b0, SFK, nAILD, SI
  // _74595 _74595_2: pin names not known; wires that end beside it: Co, _74595_2_p2, 1'b1, DCK, nDO, BD[0], BD[1], BD[2], BD[3], BD[4], BD[5], BD[6], BD[7]
  not not_6 (_74595_2_p2, nDO);
  A a_1 (
    .IN(BD), .CON({acon_1_p10[3:2], nAMR, acon_1_p10[0]}), .C_in(d_ff_as_2_q), .SI(SI), .AL(nAL), .AH(nAH),
    .SO(SO));
  D_FF_AS d_ff_as_2 (.Set(~1'b1), .D(Co), .C(SFK), .Clr(~nCAI), .Q(d_ff_as_2_q));  // open: nQ
  // _74181 _74181: pin names not known; wires that end beside it: nAL[0], nAL[1], nAL[2], nAL[3], nBL[0], nBL[1], nBL[2], nBL[3], S[0], S[1], S[2], S[3], _74181_p16[0], _74181_p16[1], _74181_p16[2], _74181_p16[3]
  // _74181 _74181_2: pin names not known; wires that end beside it: MOU, CIN, nAH[0], nAH[1], nAH[2], nAH[3], nBH[0], nBH[1], nBH[2], nBH[3], S[0], S[1], S[2], S[3], MOU, C_half, Z, C_half, _74181_2_p19[0], _74181_2_p19[1], _74181_2_p19[2], _74181_2_p19[3], Z, Co
  // _74540 _74540_1: pin names not known; wires that end beside it: _74181_p16[0], _74181_p16[1], _74181_p16[2], _74181_p16[3], _74181_2_p19[0], _74181_2_p19[1], _74181_2_p19[2], _74181_2_p19[3], nUO, nUO, BD[0], BD[1], BD[2], BD[3], BD[4], BD[5], BD[6], BD[7]
  assign not_7_out = ~{_74181_2_p19, _74181_p16};  // Not not_7, 8 bits wide
  // Probe on not_7_out
  PullUp pullup_1 (.out(Z));
  assign A = ~{nAH, nAL};  // Not not_8, 8 bits wide
  assign B = ~{nBH, nBL};  // Not not_9, 8 bits wide
  OV ov_1 (.nAH(nAH[3]), .nBH(nBH[3]), .nF3(_74181_2_p19[3]), .OV(OV));

  // Other names for the same wires on the sheet: BUS_t[7:0] = BD; CLK = C

  // Notes on the sheet:
  //   P: default 127
  //   O: default 127
  //   created by Left Hand... 
  //   An open sourse mirco computer
endmodule

/* Test case M:
C BUS P O BD A B Co
 let a = 245;
 let b = 255;
C 0x00 002 4 X X X X
C 0X00 006 4 X X X X 
C (a)  007 4 X X X X 
C (b)  011 4 X X X X 
C 0X00 004 4 X X X X
C 0XC9 017 4 X X X X 
C Z    013 4 X X X X 
C Z    016 4 X X X X 
C Z    015 0 X X X X 
C Z    001 0 X X X X 
C Z    001 0 X X X X 
C Z    001 0 X X X X 
C Z    001 0 X X X X 
C Z    001 0 X X X X 
C Z    001 0 X X X X 
C Z    001 0 X X X X 
C Z    001 0 X X X X 
C Z    001 0 X X X X 
C Z    001 0 X X X X 
C Z    001 0 X X X X 
C Z    001 0 X X X X 
C Z    001 0 X X X X 
C Z    001 0 X X X X 
C Z    001 0 X X X X 
C Z    001 0 X X X X 
C Z    001 0 X X X X 
C Z    016 2 X X X X 
*/

/* Test case D:
C BUS P O BD A B Co
 let a = 81;
 let b = 20;
C z    002 4 X X X X  #cla
C (a)  010 4 X X X X #set d
C 0    011 4 X X X X #set b able
C (b)  006 4 X X X X 
C z    012 4 X X X X  #clc
C 0x46 017 4 X X X X 
C z    003 0 X X X X  #setal
C z    001 0 X X X X 
C z    001 0 X X X X 
C z    001 0 X X X X 
C z    001 0 X X X X
C z    001 0 X X X X 
C z    001 0 X X X X 
C z    001 0 X X X X 
C z    001 0 X X X X 
C z    001 0 X X X X 
C z    001 0 X X X X 
C z    001 0 X X X X 
C z    001 0 X X X X 
C z    001 0 X X X X 
C z    001 0 X X X X 
C z    001 0 X X X X 
C z    001 0 X X X X 
C z    000 1 X X X X 
*/
