// Digital circuit MEMORY_moudle.dig as structural Verilog
module MEMORY_moudle (
  input  [7:0] DATA,
  input  INT_0,
  input  INT_1,
  input  INT_2,
  input  INT_4,
  input  INT_5,
  input  INT_6,
  input  INT_7,
  input  CLK,
  output [14:0] AD,
  output nOCS,
  output nOW,
  output nOO,
  output nACS,
  output nAW,
  output nAO,
  output [2:0] P,
  output [2:0] PS,
  output [2:0] O,
  output [2:0] OS,
  output [7:0] BUS
);

  wire _74138_2_p7, _74138_2_p8, _74138_2_p9, _74138_3_p4, _74138_5_p12, _74148_1_p10, _74148_1_p11,
       _74148_1_p12, _74148_1_p13, _74161_1_p14, _74161_2_p14, _74161_3_p14, _74161_4_p14, _74161_6_p10,
       _74161_7_p10, _74161_8_p10, _74161_9_p10, _74174_1_p2, _74174_1_p3, _74174_1_p4, _74174_1_p6,
       _74174_1_p12, _74174_1_p14, _74174_2_p2, _74174_2_p3, _74174_2_p5, _74174_2_p6, _74174_2_p14,
       _74174_3_p9, _74174_3_p10, _74174_3_p11, _74283_1_p14, and_2_out, BCK, BLD, CKE, d_ff_as_1_q,
       d_ff_as_2_q, d_ff_as_3_q, d_ff_as_4_q, d_ff_as_5_q, d_ff_as_6_q, d_ff_as_7_q, DO, DRW, FINT_3, GED,
       INT_3, MMULD, MVI, nand_3_out, nand_4_out, nand_6_out, nand_7_out, nand_8_out, nand_9_out,
       nand_10_out, nand_11_out, nBCO, nBRK, nBUSO, nINT, nINTE, nINTS, nINTU, nJ, nJC, nJMP, nJNC, nJNV,
       nJNZ, nJV, nJZ, nLDCH, nLDCL, nOJ, nor_1_out, nor_2_out, nor_3_out, nor_5_out, nor_6_out, nor_7_out,
       nor_8_out, nor_9_out, nor_11_out, nor_12_out, nor_13_out, not_1_out, not_2_out, not_3_out, not_5_out,
       not_6_out, not_7_out, not_8_out, nPCO, nRET, OLD, or_1_out, or_2_out, or_3_out, or_4_out, or_5_out,
       or_6_out, or_7_out, or_9_out, or_10_out, PCHLD, PCHO, PCLK, PCLLD, PCLO, PCMLD, PCMO, PG2, PG3, PG4,
       PLD, RD, reset_1_out, reset_2_out, reset_3_out, reset_4_out, reset_5_out, reset_6_out, reset_7_out,
       rs_ff_as_1_nq, rs_ff_as_2_nq, rs_ff_as_2_q, rs_ff_as_4_nq, rs_ff_as_5_nq, rs_ff_as_6_q, RSTC, RW,
       S_out, WT, xor_1_out, xor_2_out, xor_3_out;
  wire [3:0] _74161_4_p10, _74161_5_p10, _74574_6_p1;
  wire [7:0] _74574_1_p13, _74574_3_p11, _74574_5_p11, _74574_7_p11;

  RS_FF_AS #(.Default(1)) rs_ff_as_1 (.S(~RD), .R(~WT), .Q(RW), .nQ(rs_ff_as_1_nq));
  RS_FF_AS rs_ff_as_2 (.S(_74174_2_p2), .R(_74174_2_p6), .Q(rs_ff_as_2_q), .nQ(rs_ff_as_2_nq));
  D_FF_AS d_ff_as_1 (.Set(~1'b1), .D(1'b1), .C(~PLD), .Clr(~CLK), .Q(d_ff_as_1_q));  // open: nQ
  D_FF_AS d_ff_as_2 (.Set(~1'b1), .D(1'b1), .C(~CLK), .Clr(BLD), .Q(d_ff_as_2_q));  // open: nQ
  not not_1 (not_1_out, BUS[5]);
  not not_2 (not_2_out, BUS[6]);
  not not_3 (not_3_out, BUS[7]);
  nor nor_1 (nor_1_out, reset_1_out, _74174_1_p4);
  Reset #(.invertOutput("false")) reset_1 (.out(reset_1_out));
  nor nor_2 (nor_2_out, reset_2_out, _74174_1_p14);
  Reset #(.invertOutput("false")) reset_2 (.out(reset_2_out));
  nor nor_3 (nor_3_out, reset_3_out, _74174_2_p6);
  Reset #(.invertOutput("false")) reset_3 (.out(reset_3_out));
  nand nand_1 (nAW, rs_ff_as_1_nq, DRW);
  and and_1 (PCLK, d_ff_as_1_q, CLK, d_ff_as_2_q);
  and and_2 (and_2_out, DATA[7], rs_ff_as_4_nq, nand_9_out);
  not not_4 (nINT, _74174_1_p14);
  or or_1 (or_1_out, MVI, GED);
  nand nand_2 (DO, rs_ff_as_2_q, rs_ff_as_1_nq);
  nor nor_4 (nAO, rs_ff_as_2_nq, ~rs_ff_as_1_nq);  // NOr
  D_FF_AS d_ff_as_3 (.Set(~nRET), .D(1'b0), .C(CLK), .Clr(~nor_1_out), .Q(d_ff_as_3_q));  // open: nQ
  D_FF_AS d_ff_as_4 (.Set(~nINTS), .D(1'b0), .C(CLK), .Clr(~nor_2_out), .Q(d_ff_as_4_q));  // open: nQ
  D_FF_AS d_ff_as_5 (.Set(~or_1_out), .D(1'b0), .C(CLK), .Clr(~nor_3_out), .Q(d_ff_as_5_q));  // open: nQ
  PullUp pullup_1 (.out(nOW));
  Fuse #(.Blown("true")) fuse_1 (.A(nAW), .B(nOW));
  D_FF_AS d_ff_as_6 (.Set(~1'b1), .D(1'b1), .C(and_2_out), .Clr(~nand_9_out), .Q(d_ff_as_6_q));  // open: nQ
  or or_2 (or_2_out, nJC, not_1_out);
  or or_3 (or_3_out, nJNC, BUS[5]);
  or or_4 (or_4_out, nJZ, not_2_out);
  or or_5 (or_5_out, nJNZ, BUS[6]);
  or or_6 (or_6_out, nJV, not_3_out);
  or or_7 (or_7_out, nJNV, BUS[7]);
  or or_8 (BCK, d_ff_as_4_q, _74174_2_p2);
  D_FF_AS d_ff_as_7 (.Set(~1'b1), .D(d_ff_as_6_q), .C(CLK), .Clr(~CKE), .Q(d_ff_as_7_q));  // open: nQ
  Reset reset_4 (.out(reset_4_out));
  // _74174 _74174_1: pin names not known; wires that end beside it: d_ff_as_3_q, _74174_1_p2, _74174_1_p3, _74174_1_p4, d_ff_as_4_q, _74174_1_p6, CLK, 1'b1, _74174_1_p2, _74174_1_p3, _74174_1_p4, _74174_1_p12, _74174_1_p6, _74174_1_p14
  // _74174 _74174_2: pin names not known; wires that end beside it: d_ff_as_5_q, _74174_2_p2, _74174_2_p3, DRW, _74174_2_p5, _74174_2_p6, CLK, 1'b1, _74174_2_p2, _74174_2_p3, DRW, _74174_2_p5, _74174_2_p6, _74174_2_p14
  not not_5 (not_5_out, CLK);
  not not_6 (not_6_out, d_ff_as_7_q);
  nand nand_3 (nand_3_out, or_2_out, or_3_out, or_4_out, or_5_out, or_6_out, or_7_out, nJ, nOJ);
  not not_7 (not_7_out, nand_3_out);
  not not_8 (not_8_out, CLK);
  D_FF_AS #(.Default(1)) d_ff_as_8 (
    .Set(~not_7_out), .D(1'b0), .C(not_8_out), .Clr(~reset_4_out), .nQ(nJMP));  // open: Q
  or or_9 (or_9_out, _74174_1_p12, _74174_1_p14);
  nor nor_5 (nor_5_out, not_5_out, not_6_out);
  nor nor_6 (nor_6_out, not_5_out, d_ff_as_7_q);
  nand nand_4 (nand_4_out, RW, DRW);
  or or_10 (or_10_out, d_ff_as_6_q, rs_ff_as_6_q, MVI);
  nor nor_7 (nor_7_out, _74174_2_p5, _74174_1_p2);
  nor nor_8 (nor_8_out, _74174_2_p2, _74174_1_p12);
  nor nor_9 (nor_9_out, _74174_2_p14, or_9_out, reset_5_out);
  Reset #(.invertOutput("false")) reset_5 (.out(reset_5_out));
  nor nor_10 (nOJ, _74174_2_p6, _74174_1_p3, _74174_2_p3);
  nor nor_11 (nor_11_out, nor_5_out, nor_12_out);
  nor nor_12 (nor_12_out, nor_11_out, nor_6_out);
  nand nand_5 (BLD, nand_4_out, nand_9_out);
  nand nand_6 (nand_6_out, nINTS, nINTU);
  nand nand_7 (nand_7_out, nINTE, reset_6_out);
  Reset reset_6 (.out(reset_6_out));
  Button #(.activeLow("true")) S (.out(S_out));
  nand nand_8 (nand_8_out, not_5_out, nor_11_out);
  nand nand_9 (nand_9_out, not_5_out, nor_12_out);
  // _74148 _74148_1: pin names not known; wires that end beside it: INT_0, INT_1, INT_2, INT_3, INT_4, INT_5, INT_6, INT_7, or_10_out, _74148_1_p10, _74148_1_p11, _74148_1_p12, _74148_1_p13
  nor nor_13 (nor_13_out, d_ff_as_3_q, d_ff_as_4_q, d_ff_as_5_q);
  RS_FF_AS #(.Default(1)) rs_ff_as_3 (.S(~nor_7_out), .R(~nor_8_out), .Q(nPCO), .nQ(nBCO));
  RS_FF_AS #(.Default(1)) rs_ff_as_4 (.S(~nor_13_out), .R(~nor_9_out), .Q(MVI), .nQ(rs_ff_as_4_nq));
  RS_FF_AS #(.Default(1)) rs_ff_as_5 (.S(~S_out), .R(~nBRK), .nQ(rs_ff_as_5_nq));  // open: Q
  RS_FF_AS rs_ff_as_6 (.S(nand_6_out), .R(nand_7_out), .Q(rs_ff_as_6_q));  // open: nQ
  xor xor_1 (xor_1_out, _74148_1_p10, _74174_3_p9);
  nor nor_14 (OLD, nand_8_out, MVI, ~DATA[6]);  // NOr
  nor nor_15 (PLD, nand_8_out, MVI, DATA[6]);
  or or_11 (nINTS, _74148_1_p13, xor_1_out, xor_2_out, xor_3_out);
  xor xor_2 (xor_2_out, _74148_1_p11, _74174_3_p10);
  // _74174 _74174_3: pin names not known; wires that end beside it: _74148_1_p10, _74148_1_p11, _74148_1_p12, 1'b0, 1'b0, 1'b0, CLK, 1'b1, _74174_3_p9, _74174_3_p10, _74174_3_p11
  nor nor_16 (CKE, MVI, ~PG3, rs_ff_as_5_nq);  // NOr
  xor xor_3 (xor_3_out, _74148_1_p12, _74174_3_p11);
  // _74574 _74574_1: pin names not known; wires that end beside it: BUS[0], BUS[1], BUS[2], BUS[3], BUS[4], BUS[5], BUS[6], BUS[7], nPCO, PCLLD, _74574_1_p13[0], _74574_1_p13[1], _74574_1_p13[2], _74574_1_p13[3], _74574_1_p13[4], _74574_1_p13[5], _74574_1_p13[6], _74574_1_p13[7]
  // _74574 _74574_2: pin names not known; wires that end beside it: AD[0], AD[1], AD[2], AD[3], AD[4], AD[5], AD[6], AD[7], nBCO, BCK, _74574_1_p13[0], _74574_1_p13[1], _74574_1_p13[2], _74574_1_p13[3], _74574_1_p13[4], _74574_1_p13[5], _74574_1_p13[6], _74574_1_p13[7]
  // _74574 _74574_3: pin names not known; wires that end beside it: BUS[0], BUS[1], BUS[2], BUS[3], BUS[4], BUS[5], BUS[6], BUS[7], nPCO, PCMLD, _74574_3_p11[0], _74574_3_p11[1], _74574_3_p11[2], _74574_3_p11[3], _74574_3_p11[4], _74574_3_p11[5], _74574_3_p11[6], _74574_3_p11[7]
  // _74574 _74574_4: pin names not known; wires that end beside it: AD[8], AD[9], AD[10], AD[11], AD[12], AD[13], AD[14], nOCS, nBCO, BCK, _74574_3_p11[0], _74574_3_p11[1], _74574_3_p11[2], _74574_3_p11[3], _74574_3_p11[4], _74574_3_p11[5], _74574_3_p11[6], _74574_3_p11[7]
  // _74574 _74574_5: pin names not known; wires that end beside it: BUS[0], BUS[1], BUS[2], BUS[3], BUS[4], BUS[5], BUS[6], BUS[7], nPCO, PCHLD, _74574_5_p11[0], _74574_5_p11[1], _74574_5_p11[2], _74574_5_p11[3], _74574_5_p11[4], _74574_5_p11[5], _74574_5_p11[6], _74574_5_p11[7]
  // _74574 _74574_6: pin names not known; wires that end beside it: _74574_6_p1[0], _74574_6_p1[1], _74574_6_p1[2], _74574_6_p1[3], 1'b0, 1'b0, 1'b0, 1'b0, nBCO, BCK, _74574_5_p11[0], _74574_5_p11[1], _74574_5_p11[2], _74574_5_p11[3], _74574_5_p11[4], _74574_5_p11[5], _74574_5_p11[6], _74574_5_p11[7]
  // _74574 _74574_7: pin names not known; wires that end beside it: BUS[0], BUS[1], BUS[2], BUS[3], BUS[4], BUS[5], BUS[6], BUS[7], 1'b0, MMULD, _74574_7_p11[0], _74574_7_p11[1], _74574_7_p11[2], _74574_7_p11[3], _74574_7_p11[4], _74574_7_p11[5], _74574_7_p11[6], _74574_7_p11[7]
  // _74161 _74161_1: pin names not known; wires that end beside it: _74574_1_p13[0], _74574_1_p13[1], _74574_1_p13[2], _74574_1_p13[3], nJMP, nINT, CLK, CKE, CKE, AD[0], AD[1], AD[2], AD[3], _74161_1_p14
  // _74161 _74161_2: pin names not known; wires that end beside it: _74574_1_p13[4], _74574_1_p13[5], _74574_1_p13[6], _74574_1_p13[7], nJMP, nINT, CLK, _74161_1_p14, _74161_1_p14, AD[4], AD[5], AD[6], AD[7], _74161_2_p14
  // _74161 _74161_3: pin names not known; wires that end beside it: _74574_3_p11[0], _74574_3_p11[1], _74574_3_p11[2], _74574_3_p11[3], nJMP, nINT, CLK, _74161_2_p14, _74161_2_p14, AD[8], AD[9], AD[10], AD[11], _74161_3_p14
  // _74161 _74161_4: pin names not known; wires that end beside it: _74574_3_p11[4], _74574_3_p11[5], _74574_3_p11[6], _74574_3_p11[7], nJMP, nINT, CLK, _74161_3_p14, _74161_3_p14, _74161_4_p10[0], _74161_4_p10[1], _74161_4_p10[2], _74161_4_p10[3], _74161_4_p14
  // _74161 _74161_5: pin names not known; wires that end beside it: _74574_5_p11[0], _74574_5_p11[1], _74574_5_p11[2], _74574_5_p11[3], nJMP, nINT, CLK, _74161_4_p14, _74161_4_p14, _74161_5_p10[0], _74161_5_p10[1], _74161_5_p10[2], _74161_5_p10[3]
  // _74283 _74283_1: pin names not known; wires that end beside it: _74161_4_p10[0], _74161_4_p10[1], _74161_4_p10[2], _74161_4_p10[3], _74574_7_p11[0], _74574_7_p11[1], _74574_7_p11[2], _74574_7_p11[3], 1'b0, AD[12], AD[13], AD[14], nOCS, _74283_1_p14
  // _74283 _74283_2: pin names not known; wires that end beside it: _74161_5_p10[0], _74161_5_p10[1], _74161_5_p10[2], _74161_5_p10[3], _74574_7_p11[4], _74574_7_p11[5], _74574_7_p11[6], _74574_7_p11[7], _74283_1_p14, _74574_6_p1[0], _74574_6_p1[1], _74574_6_p1[2], _74574_6_p1[3]
  // _74244 _74244_1: pin names not known; wires that end beside it: _74574_1_p13[0], _74574_1_p13[1], _74574_1_p13[2], _74574_1_p13[3], _74574_1_p13[4], _74574_1_p13[5], _74574_1_p13[6], _74574_1_p13[7], PCLO, PCLO, BUS[0], BUS[1], BUS[2], BUS[3], BUS[4], BUS[5], BUS[6], BUS[7]
  // _74244 _74244_2: pin names not known; wires that end beside it: _74574_3_p11[0], _74574_3_p11[1], _74574_3_p11[2], _74574_3_p11[3], _74574_3_p11[4], _74574_3_p11[5], _74574_3_p11[6], _74574_3_p11[7], PCMO, PCMO, BUS[0], BUS[1], BUS[2], BUS[3], BUS[4], BUS[5], BUS[6], BUS[7]
  // _74244 _74244_3: pin names not known; wires that end beside it: _74574_5_p11[0], _74574_5_p11[1], _74574_5_p11[2], _74574_5_p11[3], _74574_5_p11[4], _74574_5_p11[5], _74574_5_p11[6], _74574_5_p11[7], PCHO, PCHO, BUS[0], BUS[1], BUS[2], BUS[3], BUS[4], BUS[5], BUS[6], BUS[7]
  // _74138 _74138: pin names not known; wires that end beside it: PS[0], PS[1], PS[2], 1'b1, 1'b0, 1'b0, PG2, PG3, PG4
  // _74138 _74138_2: pin names not known; wires that end beside it: P[0], P[1], P[2], PCLK, PG2, 1'b0, _74138_2_p7, _74138_2_p8, _74138_2_p9, nINTE, RD, WT, nINTU, GED
  // _74138 _74138_3: pin names not known; wires that end beside it: O[0], O[1], O[2], _74138_3_p4, OS[1], OS[2], nBUSO, PCLO, PCMO, PCHO
  not not_9 (_74138_3_p4, OS[0]);
  // _74138 _74138_4: pin names not known; wires that end beside it: P[0], P[1], P[2], PCLK, PG3, 1'b0, nJ, nBRK, nJC, nJNC, nJZ, nJNZ, nJV, nJNV
  // _74138 _74138_5: pin names not known; wires that end beside it: P[0], P[1], P[2], PCLK, PG4, 1'b0, nRET, RSTC, nLDCL, nLDCH, FINT_3, _74138_5_p12
  not not_10 (PCLLD, _74138_2_p7);
  not not_11 (PCMLD, _74138_2_p8);
  not not_12 (PCHLD, _74138_2_p9);
  not not_13 (MMULD, _74138_5_p12);
  // Probe on AD
  not not_14 (nACS, nOCS);
  // _74574 _74574_8: pin names not known; wires that end beside it: BUS[0], BUS[1], BUS[2], BUS[3], BUS[4], BUS[5], BUS[6], BUS[7], DO, BCK, DATA[0], DATA[1], DATA[2], DATA[3], DATA[4], DATA[5], DATA[6], DATA[7]
  // _74161 _74161_6: pin names not known; wires that end beside it: BUS[0], BUS[1], BUS[2], BUS[3], nLDCL, 1'b1, CLK, 1'b1, 1'b1, _74161_6_p10
  // _74161 _74161_7: pin names not known; wires that end beside it: BUS[4], BUS[5], BUS[6], BUS[7], nLDCL, 1'b1, CLK, _74161_6_p10, _74161_6_p10, _74161_7_p10
  nand nand_10 (nand_10_out, ~_74161_9_p10, FINT_3);  // NAnd
  nand nand_11 (nand_11_out, RSTC, reset_7_out);
  Reset reset_7 (.out(reset_7_out));
  // Probe on DATA
  RS_FF_AS rs_ff_as_7 (.S(nand_10_out), .R(nand_11_out), .nQ(INT_3));  // open: Q
  // _74174 _74174_4: pin names not known; wires that end beside it: DATA[0], DATA[1], DATA[2], DATA[3], DATA[4], DATA[5], PLD, 1'b1, P[0], P[1], P[2], PS[0], PS[1], PS[2]
  // _74174 _74174_5: pin names not known; wires that end beside it: DATA[0], DATA[1], DATA[2], DATA[3], DATA[4], DATA[5], OLD, 1'b1, O[0], O[1], O[2], OS[0], OS[1], OS[2]
  // _74574 _74574_9: pin names not known; wires that end beside it: DATA[0], DATA[1], DATA[2], DATA[3], DATA[4], DATA[5], DATA[6], DATA[7], nBUSO, BLD, BUS[0], BUS[1], BUS[2], BUS[3], BUS[4], BUS[5], BUS[6], BUS[7]
  // _74161 _74161_8: pin names not known; wires that end beside it: BUS[0], BUS[1], BUS[2], BUS[3], nLDCH, 1'b1, CLK, _74161_7_p10, _74161_7_p10, _74161_8_p10
  // _74161 _74161_9: pin names not known; wires that end beside it: BUS[4], BUS[5], BUS[6], BUS[7], nLDCH, 1'b1, CLK, _74161_8_p10, _74161_8_p10, _74161_9_p10
  // Probe on {PS, P}
  // Probe on {OS, O}

  assign nOO = nAO;

  // Other names for the same wires on the sheet: D6 = DATA[6]; D7 = DATA[7]; RAMWE = nAW; RAMOE = nAO; ROMOE = nAO;
  //   ROMWE = nOW

  // Notes on the sheet:
  //   INT_0: default 1
  //   INT_1: default 1
  //   INT_2: default 1
  //   INT_4: default 1
  //   INT_5: default 1
  //   INT_6: default 1
  //   INT_7: default 1
endmodule
