// Digital circuit VGA_moudle.dig as structural Verilog
module VGA_moudle (
  input  [7:0] BUS,
  input  [2:0] P,
  input  [2:0] PS,
  input  CLK,
  input  C,
  output [2:0] R,
  output [2:0] G,
  output [2:0] B,
  output H,
  output V
);

  wire _74161_1_p14, _74161_2_p14, _74161_3_p14, _74161_5_p14, _74161_6_p14, _74161_8_p14, _74161_9_p14,
       _74283_1_p14, _74688_1_p18, _74688_2_p18, _74688_3_p18, _74688_4_p18, _74688_5_p18, and_1_out,
       and_2_out, CPV, d_ff_as_1_q, d_ff_as_2_q, d_ff_as_3_q, d_ff_as_4_q, d_ff_as_5_nq, HB, HCPE, HR, HS,
       nand_1_out, nand_2_out, nand_6_out, nand_7_out, nand_9_out, nand_11_out, nand_12_out, nHR, nIVS, nLX,
       nLXB, nLY, nLYB, nor_1_out, nor_2_out, nor_3_out, nor_4_out, nor_6_out, nor_8_out, nor_9_out,
       not_2_out, not_3_out, not_4_out, nSAM, nSEL, nVR, nWR, nYP, or_4_out, or_5_out, or_6_out, SEL, VB,
       VCPE, VF, VS, WE0, WE1, XO, YO;
  wire [0:0] _74161_5_p10, _74161_8_p10;
  wire [1:0] B_t;
  wire [2:0] G_t, R_t;
  wire [3:0] _74161_1_p10, _74161_2_p10, _74161_3_p10, _74161_4_p10, _74244_1_p11, _74244_1_p15,
       _74244_2_p11, _74244_2_p15, _74273_1_p14, _74273_1_p18, _74283_1_p13, _74283_2_p10;
  wire [3:2] _74161_7_p12, _74161_10_p12;
  wire [7:0] XAD, YAD;
  wire [7:7] _74157_4_p14, _74157_8_p14;
  wire [14:0] _74157_1_p11, _74157_5_p11;

  nand nand_1 (nand_1_out, VB, VB);
  nand nand_2 (nand_2_out, HR, HR);
  D_FF_AS #(.Default(1)) d_ff_as_1 (.Set(~1'b1), .D(1'b1), .C(nLX), .Clr(~nLXB), .Q(d_ff_as_1_q));  // open: nQ
  D_FF_AS #(.Default(1)) d_ff_as_2 (.Set(~nLX), .D(1'b0), .C(nLXB), .Clr(~1'b1), .Q(d_ff_as_2_q));  // open: nQ
  D_FF_AS #(.Default(1)) d_ff_as_3 (.Set(~1'b1), .D(1'b1), .C(nLY), .Clr(~nLYB), .Q(d_ff_as_3_q));  // open: nQ
  D_FF_AS #(.Default(1)) d_ff_as_4 (.Set(~nLY), .D(1'b0), .C(nLYB), .Clr(~1'b1), .Q(d_ff_as_4_q));  // open: nQ
  nor nor_1 (nor_1_out, CPV, VB);
  nor nor_2 (nor_2_out, CPV, nand_1_out);
  nor nor_3 (nor_3_out, C, HR);
  nor nor_4 (nor_4_out, C, nand_2_out);
  nor nor_5 (VCPE, nor_1_out, nor_6_out);
  nor nor_6 (nor_6_out, VCPE, nor_2_out);
  nor nor_7 (HCPE, nor_3_out, nor_8_out);
  nor nor_8 (nor_8_out, HCPE, nor_4_out);
  and and_1 (and_1_out, d_ff_as_2_q, nWR);
  and and_2 (and_2_out, d_ff_as_4_q, nWR);
  nand nand_3 (nVR, CPV, nor_6_out);
  nand nand_4 (nHR, C, nor_8_out);
  nand nand_5 (CPV, nHR, nHR);
  // _74273 _74273_1: pin names not known; wires that end beside it: BUS[0], BUS[1], BUS[2], BUS[3], BUS[4], BUS[5], BUS[6], BUS[7], nYP, 1'b1, _74273_1_p14[0], _74273_1_p14[1], _74273_1_p14[2], _74273_1_p14[3], _74273_1_p18[0], _74273_1_p18[1], _74273_1_p18[2], _74273_1_p18[3]
  // _74161 _74161_1: pin names not known; wires that end beside it: BUS[0], BUS[1], BUS[2], BUS[3], d_ff_as_1_q, 1'b1, and_1_out, d_ff_as_2_q, d_ff_as_2_q, _74161_1_p10[0], _74161_1_p10[1], _74161_1_p10[2], _74161_1_p10[3], _74161_1_p14
  // _74161 _74161_2: pin names not known; wires that end beside it: BUS[4], BUS[5], BUS[6], BUS[7], d_ff_as_1_q, 1'b1, and_1_out, _74161_1_p14, _74161_1_p14, _74161_2_p10[0], _74161_2_p10[1], _74161_2_p10[2], _74161_2_p10[3], _74161_2_p14
  // _74161 _74161_3: pin names not known; wires that end beside it: BUS[0], BUS[1], BUS[2], BUS[3], d_ff_as_3_q, 1'b1, and_2_out, _74161_2_p14, _74161_2_p14, _74161_3_p10[0], _74161_3_p10[1], _74161_3_p10[2], _74161_3_p10[3], _74161_3_p14
  // _74161 _74161_4: pin names not known; wires that end beside it: BUS[4], BUS[5], BUS[6], BUS[7], d_ff_as_3_q, 1'b1, and_2_out, _74161_3_p14, _74161_3_p14, _74161_4_p10[0], _74161_4_p10[1], _74161_4_p10[2], _74161_4_p10[3]
  not not_1 (nSEL, SEL);
  // _74283 _74283_1: pin names not known; wires that end beside it: _74273_1_p14[0], _74273_1_p14[1], _74273_1_p14[2], _74273_1_p14[3], YAD[0], YAD[1], YAD[2], YAD[3], 1'b0, _74283_1_p13[0], _74283_1_p13[1], _74283_1_p13[2], _74283_1_p13[3], _74283_1_p14
  // _74283 _74283_2: pin names not known; wires that end beside it: _74273_1_p18[0], _74273_1_p18[1], _74273_1_p18[2], _74273_1_p18[3], YAD[4], YAD[5], YAD[6], YAD[7], _74283_1_p14, _74283_2_p10[0], _74283_2_p10[1], _74283_2_p10[2], _74283_2_p10[3]
  // _74157 _74157_1: pin names not known; wires that end beside it: _74161_1_p10[0], _74161_1_p10[1], _74161_1_p10[2], _74161_1_p10[3], XAD[0], XAD[1], XAD[2], XAD[3], nSEL, 1'b0, _74157_1_p11[0], _74157_1_p11[1], _74157_1_p11[2], _74157_1_p11[3]
  // _74157 _74157_2: pin names not known; wires that end beside it: _74161_2_p10[0], _74161_2_p10[1], _74161_2_p10[2], _74161_2_p10[3], XAD[4], XAD[5], XAD[6], XAD[7], nSEL, 1'b0, _74157_1_p11[4], _74157_1_p11[5], _74157_1_p11[6], _74157_1_p11[7]
  // _74157 _74157_3: pin names not known; wires that end beside it: _74161_3_p10[0], _74161_3_p10[1], _74161_3_p10[2], _74161_3_p10[3], _74283_1_p13[0], _74283_1_p13[1], _74283_1_p13[2], _74283_1_p13[3], nSEL, 1'b0, _74157_1_p11[8], _74157_1_p11[9], _74157_1_p11[10], _74157_1_p11[11]
  // _74157 _74157_4: pin names not known; wires that end beside it: _74161_4_p10[0], _74161_4_p10[1], _74161_4_p10[2], _74161_4_p10[3], _74283_2_p10[0], _74283_2_p10[1], _74283_2_p10[2], _74283_2_p10[3], nSEL, 1'b0, _74157_1_p11[12], _74157_1_p11[13], _74157_1_p11[14], _74157_4_p14[7]
  // _74157 _74157_5: pin names not known; wires that end beside it: _74161_1_p10[0], _74161_1_p10[1], _74161_1_p10[2], _74161_1_p10[3], XAD[0], XAD[1], XAD[2], XAD[3], SEL, 1'b0, _74157_5_p11[0], _74157_5_p11[1], _74157_5_p11[2], _74157_5_p11[3]
  // _74157 _74157_6: pin names not known; wires that end beside it: _74161_2_p10[0], _74161_2_p10[1], _74161_2_p10[2], _74161_2_p10[3], XAD[4], XAD[5], XAD[6], XAD[7], SEL, 1'b0, _74157_5_p11[4], _74157_5_p11[5], _74157_5_p11[6], _74157_5_p11[7]
  // _74157 _74157_7: pin names not known; wires that end beside it: _74161_3_p10[0], _74161_3_p10[1], _74161_3_p10[2], _74161_3_p10[3], _74283_1_p13[0], _74283_1_p13[1], _74283_1_p13[2], _74283_1_p13[3], SEL, 1'b0, _74157_5_p11[8], _74157_5_p11[9], _74157_5_p11[10], _74157_5_p11[11]
  // _74157 _74157_8: pin names not known; wires that end beside it: _74161_4_p10[0], _74161_4_p10[1], _74161_4_p10[2], _74161_4_p10[3], _74283_2_p10[0], _74283_2_p10[1], _74283_2_p10[2], _74283_2_p10[3], SEL, 1'b0, _74157_5_p11[12], _74157_5_p11[13], _74157_5_p11[14], _74157_8_p14[7]
  // _74161 _74161_5: pin names not known; wires that end beside it: 1'b0, 1'b0, 1'b0, 1'b0, 1'b1, nVR, CPV, VCPE, VCPE, _74161_5_p10[0], YAD[0], YAD[1], YAD[2], _74161_5_p14
  // _74161 _74161_6: pin names not known; wires that end beside it: 1'b0, 1'b0, 1'b0, 1'b0, 1'b1, nVR, CPV, _74161_5_p14, _74161_5_p14, YAD[3], YAD[4], YAD[5], YAD[6], _74161_6_p14
  // _74161 _74161_7: pin names not known; wires that end beside it: 1'b0, 1'b0, 1'b0, 1'b0, 1'b1, nVR, CPV, _74161_6_p14, _74161_6_p14, YAD[7], YO, _74161_7_p12[2], _74161_7_p12[3]
  // _74244 _74244_1: pin names not known; wires that end beside it: BUS[0], BUS[1], BUS[2], BUS[3], BUS[4], BUS[5], BUS[6], BUS[7], nSEL, nSEL, _74244_1_p11[0], _74244_1_p11[1], _74244_1_p11[2], _74244_1_p11[3], _74244_1_p15[0], _74244_1_p15[1], _74244_1_p15[2], _74244_1_p15[3]
  // _74244 _74244_2: pin names not known; wires that end beside it: BUS[0], BUS[1], BUS[2], BUS[3], BUS[4], BUS[5], BUS[6], BUS[7], SEL, SEL, _74244_2_p11[0], _74244_2_p11[1], _74244_2_p11[2], _74244_2_p11[3], _74244_2_p15[0], _74244_2_p15[1], _74244_2_p15[2], _74244_2_p15[3]
  // Probe on {YO, YAD, _74161_5_p10[0]}
  nor nor_9 (nor_9_out, XO, YO);
  // _74688 _74688_1: pin names not known; wires that end beside it: _74161_5_p10[0], YAD[0], YAD[1], YAD[2], YAD[3], YAD[4], YAD[5], YAD[6], 1'b0, 1'b1, 1'b0, 1'b1, 1'b0, 1'b1, 1'b1, 1'b1, YO, _74688_1_p18
  or or_1 (VF, _74688_1_p18, ~YAD[7]);  // Or
  // _74688 _74688_2: pin names not known; wires that end beside it: _74161_5_p10[0], YAD[0], YAD[1], YAD[2], YAD[3], YAD[4], YAD[5], YAD[6], 1'b0, 1'b0, 1'b1, 1'b1, 1'b0, 1'b1, 1'b1, 1'b1, YO, _74688_2_p18
  or or_2 (VS, _74688_2_p18, ~YAD[7]);  // Or
  // _74688 _74688_3: pin names not known; wires that end beside it: _74161_5_p10[0], YAD[0], YAD[1], YAD[2], YAD[3], YAD[4], YAD[5], YAD[6], 1'b0, 1'b0, 1'b1, 1'b1, 1'b0, 1'b0, 1'b0, 1'b0, YAD[7], _74688_3_p18
  or or_3 (VB, _74688_3_p18, ~YO);  // Or
  or or_4 (or_4_out, _74157_4_p14[7], SEL);
  nand nand_6 (nand_6_out, _74157_8_p14[7], SEL);
  assign R = nor_9_out ? R_t : 3'bz;  // Driver driver_1
  assign B[2:1] = nor_9_out ? B_t : 2'bz;  // Driver driver_2
  assign G = nor_9_out ? G_t : 3'bz;  // Driver driver_3
  not not_2 (not_2_out, _74157_4_p14[7]);
  or or_5 (or_5_out, ~_74157_4_p14[7], SEL);  // Or
  or or_6 (or_6_out, _74157_8_p14[7], ~SEL);  // Or
  not not_3 (not_3_out, _74157_8_p14[7]);
  RAMSinglePortSel #(.AddrBits(15), .Bits(8)) ramsingleportsel_1 (
    .A(_74157_1_p11), .CS(~_74157_4_p14[7]), .WE(~WE0), .OE(~or_4_out), .D({_74244_1_p15, _74244_1_p11}));
  RAMSinglePortSel #(.AddrBits(15), .Bits(8)) ramsingleportsel_2 (
    .A(_74157_1_p11), .CS(~not_2_out), .WE(~WE0), .OE(~or_5_out), .D({_74244_1_p15, _74244_1_p11}));
  RAMSinglePortSel #(.AddrBits(15), .Bits(8)) ramsingleportsel_3 (
    .A(_74157_5_p11), .CS(~_74157_8_p14[7]), .WE(~WE1), .OE(~or_6_out), .D({_74244_2_p15, _74244_2_p11}));
  RAMSinglePortSel #(.AddrBits(15), .Bits(8)) ramsingleportsel_4 (
    .A(_74157_5_p11), .CS(~not_3_out), .WE(~WE1), .OE(~nand_6_out), .D({_74244_2_p15, _74244_2_p11}));
  // _74161 _74161_8: pin names not known; wires that end beside it: 1'b0, 1'b0, 1'b0, 1'b0, 1'b1, nHR, C, HCPE, HCPE, _74161_8_p10[0], XAD[0], XAD[1], XAD[2], _74161_8_p14
  // _74161 _74161_9: pin names not known; wires that end beside it: 1'b0, 1'b0, 1'b0, 1'b0, 1'b1, nHR, C, _74161_8_p14, _74161_8_p14, XAD[3], XAD[4], XAD[5], XAD[6], _74161_9_p14
  // _74161 _74161_10: pin names not known; wires that end beside it: 1'b0, 1'b0, 1'b0, 1'b0, 1'b1, nHR, C, _74161_9_p14, _74161_9_p14, XAD[7], XO, _74161_10_p12[2], _74161_10_p12[3]
  nand nand_7 (nand_7_out, HS, H);
  nand nand_8 (H, nand_7_out, HB);
  nand nand_9 (nand_9_out, VF, V);
  nand nand_10 (V, nand_9_out, VS);
  D_FF_AS #(.Default(1)) d_ff_as_5 (.Set(~nSAM), .D(d_ff_as_5_nq), .C(nIVS), .Clr(~1'b1), .Q(SEL), .nQ(d_ff_as_5_nq));
  or or_7 (WE1, nWR, SEL);
  or or_8 (WE0, nWR, ~SEL);  // Or
  // Probe on {_74244_1_p15, _74244_1_p11}
  // Probe on {_74244_2_p15, _74244_2_p11}
  not not_4 (not_4_out, PS[0]);
  nand nand_11 (nand_11_out, PS[1], PS[2]);
  // Probe on {XO, XAD, _74161_8_p10[0]}
  // _74157 _74157_9: pin names not known; wires that end beside it: _74244_1_p11[0], _74244_1_p11[1], _74244_1_p11[2], _74244_1_p11[3], _74244_2_p11[0], _74244_2_p11[1], _74244_2_p11[2], _74244_2_p11[3], SEL, 1'b0, R_t[0], R_t[1], R_t[2], B_t[0]
  // _74157 _74157_10: pin names not known; wires that end beside it: _74244_1_p15[0], _74244_1_p15[1], _74244_1_p15[2], _74244_1_p15[3], _74244_2_p15[0], _74244_2_p15[1], _74244_2_p15[2], _74244_2_p15[3], SEL, 1'b0, B_t[1], G_t[0], G_t[1], G_t[2]
  nand nand_12 (nand_12_out, XAD[7], XO);
  // _74138 _74138_1: pin names not known; wires that end beside it: P[0], P[1], P[2], CLK, not_4_out, nand_11_out, nSAM, nIVS, nWR, nYP, nLXB, nLX, nLYB, nLY
  // _74688 _74688_4: pin names not known; wires that end beside it: _74161_8_p10[0], XAD[0], XAD[1], XAD[2], XAD[3], XAD[4], XAD[5], XAD[6], 1'b0, 1'b0, 1'b0, 1'b0, 1'b1, 1'b0, 1'b1, 1'b0, XAD[7], _74688_4_p18
  or or_9 (HS, _74688_4_p18, ~XO);  // Or
  // _74688 _74688_5: pin names not known; wires that end beside it: _74161_8_p10[0], XAD[0], XAD[1], XAD[2], XAD[3], XAD[4], XAD[5], XAD[6], 1'b0, 1'b0, 1'b0, 1'b0, 1'b1, 1'b1, 1'b0, 1'b1, XAD[7], _74688_5_p18
  or or_10 (HB, _74688_5_p18, ~XO);  // Or
  // _74688 _74688_6: pin names not known; wires that end beside it: _74161_8_p10[0], XAD[0], XAD[1], XAD[2], XAD[3], XAD[4], XAD[5], XAD[6], 1'b1, 1'b1, 1'b1, 1'b1, 1'b1, 1'b0, 1'b0, 1'b0, nand_12_out, HR

  assign B[0] = 1'b0;

  // Other names for the same wires on the sheet: BO[2:1] = B[2:1]; CPH = C; GO[2:0] = G; HSY = H; RO[2:0] = R;
  //   VSY = V

  // Notes on the sheet:
  //   C: Hz: 2147483647
  //   MADE BY LEFT HAND 
  //   an open sourse 74 gate computer
  //   VGA display card
endmodule
