// Digital circuit POB.dig as structural Verilog
module POB (
  input  in_1,
  input  clk,
  input  clk_2
);

  wire _74138_3_p7, _74138_3_p8, _74138_3_p9, _74138_5_p11, _74138_5_p12, _74138_8_p12, _74138_8_p13,
       _74138_10_p14, _74138_p7, _74138_p8, _74138_p9, _74138_p10, _74138_p11, _74148_1_p10, _74148_1_p11,
       _74148_1_p12, _74148_1_p13, _74161_2_p14, _74161_4_p14, _74161_5_p14, _74161_6_p14, _74161_8_p10,
       _74161_9_p10, _74161_10_p10, _74161_11_p10, _74161_12_p10, _74161_13_p10, _74161_14_p10,
       _74161_15_p10, _74161_16_p14, _74161_17_p14, _74161_18_p14, _74161_20_p14, _74161_21_p14,
       _74161_23_p14, _74161_24_p14, _74161_p14, _74165_1_p13, _74165_1_p14, _74165_1_p15, _74165_1_p16,
       _74165_2_p14, _74165_2_p15, _74174_2_p9, _74174_2_p10, _74174_2_p11, _74174_3_p9, _74174_3_p10,
       _74181_2_p17, _74181_2_p23, _74273_p16, _74283_1_p14, _74595_1_p14, _74595_2_p2, _74595_2_p14,
       _74688_1_p18, _74688_2_p18, _74688_3_p18, _74688_4_p18, _74688_5_p18, ACLD, ACP, and_1_out, and_6_out,
       and_8_out, and_9_out, and_10_out, AOW, BCIR0, BCIR1, BCIR2, BCK_0, BHLD, BLD, BLLD, C_half, C_out, Ci,
       CIR0, CIR1, CIR2, CIR3, CIR4, CIR5, CKE, CLK_t, Co, CPH, CPV, CRO, CTC, CTI, D6, D7, d_ff_1_nq,
       d_ff_1_q, d_ff_as_1_q, d_ff_as_5_q, d_ff_as_6_q, d_ff_as_7_nq, d_ff_as_7_q, d_ff_as_8_nq,
       d_ff_as_9_nq, d_ff_as_10_q, d_ff_as_11_q, d_ff_as_13_q, d_ff_as_14_q, d_ff_as_15_q, d_ff_as_16_q,
       d_ff_as_17_q, d_ff_as_18_q, d_ff_as_19_q, d_ff_as_20_q, d_ff_as_21_nq, DCK, DIV, DRO, DTO, GED, HB,
       HCPE, HR, HS, HSY, INT_1, INT_2, INT_3, INT_4, INT_5, INT_6, INT_7, INTO, IO0O, IO1O, K_out, M, MCK,
       MUL, MVI, nACO, nACP, nAILD, nAMR, nand_1_out, nand_2_out, nand_5_out, nand_6_out, nand_7_out,
       nand_9_out, nand_10_out, nand_14_out, nand_15_out, nand_19_out, nand_20_out, nand_22_out, nand_24_out,
       nand_25_out, nAOO, nBCO_0, nBCO_1, nBUSO, nCAI, nCLC, nDO, nF7, nFBK, nHLT, nHR, nINT, nINT_3, nINTS,
       nIVS, nJC, nJMP, nJMP_I, nJNC, nJNV, nJNZ, nJV, nJZ, nLDM, nLX, nLXB, nLY, nLYB, nMLD, nNF, nor_1_out,
       nor_2_out, nor_3_out, nor_4_out, nor_5_out, nor_6_out, nor_7_out, nor_8_out, nor_9_out, nor_14_out,
       nor_15_out, nor_16_out, nor_18_out, nor_19_out, nor_20_out, nor_21_out, nor_23_out, nor_25_out,
       nor_26_out, not_2_out, not_3_out, not_4_out, not_6_out, not_7_out, not_8_out, not_9_out, not_10_out,
       not_11_out, not_13_out, not_19_out, not_20_out, not_21_out, not_23_out, not_26_out, not_38_out,
       not_39_out, not_40_out, nPCO, nREC, nRET, nRST, nSAM, nSEL, nSTC, nSTL, nSTR, nT0HLD, nT0LLD, nT1HLD,
       nT1LLD, nUO, nVR, nWVGA, nYP, OLD, or_1_out, or_2_out, or_7_out, or_8_out, or_9_out, or_10_out,
       or_11_out, or_12_out, or_18_out, or_19_out, or_20_out, OV, PCHLD, PCHO, PCLK, PCLLD, PCLO, PCMLD,
       PCMO, PG0, PG1, PG2, PG3, PG4, PG5, PLD, pullup_1_out, RAMO, RD, RDTO, reset_1_out, reset_2_out,
       reset_3_out, rs_ff_as_1_nq, rs_ff_as_1_q, rs_ff_as_2_nq, rs_ff_as_2_q, rs_ff_as_3_nq, rs_ff_as_3_q,
       rs_ff_as_4_q, rs_ff_as_5_q, rs_ff_as_6_nq, rs_ff_as_6_q, S0, S1, SEL, SFK, SI, SO, ULK, VB, VCPE, VF,
       VS, VSY, WE0, WE1, WT, XO, xor_1_out, xor_2_out, xor_3_out, YO, Z;
  wire [0:0] _74161_20_p10, _74161_23_p10;
  wire [1:0] B;
  wire [2:0] _74181_2_p19, G, GO, O, OS, P, PS, R, RO;
  wire [2:1] BO;
  wire [3:0] _74157_1_p11, _74157_2_p11, _74157_3_p11, _74157_4_p11, _74157_5_p11, _74157_6_p11,
       _74157_7_p11, _74157_8_p11, _74161_16_p10, _74161_17_p10, _74161_18_p10, _74161_19_p10, _74181_p16,
       _74195_p8, _74273_2_p14, _74273_2_p18, _74283_1_p13, _74283_2_p11, nAH, nAL, nBH, nBL, not_30_out,
       not_31_out, not_32_out, not_33_out, S;
  wire [3:1] _74195_p6;
  wire [3:2] _74161_22_p12, _74161_25_p12;
  wire [5:0] DT;
  wire [7:0] _74244_8_p11, _74244_9_p11, _74574_4_p11, _74574_5_p11, _74574_7_p11, _74574_10_p11,
       _74574_16_p18, _74574_p11, BUS, not_35_out, XAD, YAD;
  wire [7:7] _74574_10_p8;
  wire [15:0] AD;
  wire [22:16] _74574_10_p1;

  or or_1 (or_1_out, BCIR1, BCIR2);
  or or_2 (or_2_out, GED, MVI);
  nor nor_1 (nor_1_out, reset_1_out, CIR2);
  Reset #(.invertOutput("false")) reset_1 (.out(reset_1_out));
  nor nor_2 (nor_2_out, reset_2_out, CIR4);
  Reset #(.invertOutput("false")) reset_2 (.out(reset_2_out));
  Reset #(.invertOutput("false")) reset_3 (.out(reset_3_out));
  nor nor_3 (nor_3_out, reset_3_out, CIR5);
  not not_1 (nINT, CIR5);
  D_FF_AS d_ff_as_1 (.Set(~1'b1), .D(1'b1), .C(~PLD), .Clr(~CLK_t), .Q(d_ff_as_1_q));  // open: nQ
  and and_1 (and_1_out, D7, d_ff_as_8_nq, nand_2_out);
  RS_FF_AS #(.Default(1)) rs_ff_as_1 (.S(CIR0), .R(CIR1), .Q(rs_ff_as_1_q), .nQ(rs_ff_as_1_nq));
  RS_FF_AS #(.Default(1)) rs_ff_as_2 (.S(CIR0), .R(or_1_out), .Q(rs_ff_as_2_q), .nQ(rs_ff_as_2_nq));
  and and_2 (PCLK, d_ff_as_1_q, CLK_t);
  or or_3 (BCK_0, ~nFBK, BCIR1);  // Or
  D_FF_AS d_ff_as_2 (.Set(~or_2_out), .D(1'b0), .C(CLK_t), .Clr(~nor_1_out), .Q(BCIR0));  // open: nQ
  D_FF_AS d_ff_as_3 (.Set(~nRET), .D(1'b0), .C(CLK_t), .Clr(~nor_2_out), .Q(BCIR1));  // open: nQ
  D_FF_AS d_ff_as_4 (.Set(~nINTS), .D(1'b0), .C(CLK_t), .Clr(~nor_3_out), .Q(BCIR2));  // open: nQ
  D_FF_AS d_ff_as_5 (.Set(~1'b1), .D(1'b1), .C(and_1_out), .Clr(~nand_2_out), .Q(d_ff_as_5_q));  // open: nQ
  or or_4 (nBCO_0, rs_ff_as_1_q, rs_ff_as_2_q, ~PG3);  // Or
  and and_3 (nPCO, PG3, rs_ff_as_1_nq);
  or or_5 (nBCO_1, rs_ff_as_1_q, rs_ff_as_2_nq, ~PG3);  // Or
  D_FF_AS d_ff_as_6 (.Set(~1'b1), .D(d_ff_as_5_q), .C(CLK_t), .Clr(~CKE), .Q(d_ff_as_6_q));  // open: nQ
  not not_2 (not_2_out, CLK_t);
  not not_3 (not_3_out, d_ff_as_6_q);
  nor nor_4 (nor_4_out, BCIR0, BCIR1, BCIR2);
  nor nor_5 (nor_5_out, CIR2, CIR4, CIR5);
  // _74174 _74174: pin names not known; wires that end beside it: BCIR0, CIR0, CIR1, BCIR1, CIR3, BCIR2, CLK_t, 1'b1, CIR0, CIR1, CIR2, CIR3, CIR4, CIR5
  nor nor_6 (nor_6_out, not_2_out, not_3_out);
  nor nor_7 (nor_7_out, not_2_out, d_ff_as_6_q);
  LED led_1 (.in(CIR0));
  nor nor_8 (nor_8_out, nor_6_out, nor_9_out);
  nor nor_9 (nor_9_out, nor_8_out, nor_7_out);
  LED led_2 (.in(CIR2));
  LED led_3 (.in(CIR1));
  RS_FF_AS rs_ff_as_3 (.S(CIR2), .R(CIR0), .Q(rs_ff_as_3_q), .nQ(rs_ff_as_3_nq));
  D_FF_AS #(.Default(1)) d_ff_as_7 (.Set(~WT), .D(1'b0), .C(nRST), .Clr(~RD), .Q(d_ff_as_7_q), .nQ(d_ff_as_7_nq));
  D_FF_AS #(.Default(1)) d_ff_as_8 (.Set(~nor_4_out), .D(1'b0), .C(nRST), .Clr(~nor_5_out), .Q(MVI), .nQ(d_ff_as_8_nq));
  RS_FF_AS rs_ff_as_4 (.S(~nHLT), .R(~ULK), .Q(rs_ff_as_4_q));  // open: nQ
  nand nand_1 (nand_1_out, not_2_out, nor_8_out);
  nand nand_2 (nand_2_out, not_2_out, nor_9_out);
  LED led_4 (.in(CIR3));
  LED led_5 (.in(CIR4));
  nor nor_10 (RAMO, rs_ff_as_3_q, d_ff_as_7_nq);
  nand nand_3 (DTO, rs_ff_as_3_nq, d_ff_as_7_q);
  nand nand_4 (AOW, d_ff_as_7_q, CIR1);
  nor nor_11 (CKE, MVI, rs_ff_as_4_q);
  not not_4 (not_4_out, CKE);
  nor nor_12 (OLD, nand_1_out, not_4_out, ~D6);  // NOr
  nor nor_13 (PLD, nand_1_out, not_4_out, D6);
  not not_5 (BLD, nand_2_out);
  LED led_6 (.in(CIR5));
  D_FF_AS d_ff_as_9 (.Set(~nor_14_out), .D(BUS[0]), .C(CTI), .Clr(~nINTS), .nQ(d_ff_as_9_nq));  // open: Q
  // _74148 _74148_1: pin names not known; wires that end beside it: 1'b1, INT_1, INT_2, INT_3, INT_4, INT_5, INT_6, INT_7, 1'b0, _74148_1_p10, _74148_1_p11, _74148_1_p12, _74148_1_p13
  xor xor_1 (xor_1_out, _74148_1_p10, _74174_2_p9);
  or or_6 (nINTS, _74148_1_p13, d_ff_as_9_nq, MVI);
  xor xor_2 (xor_2_out, _74148_1_p11, _74174_2_p10);
  // _74174 _74174_2: pin names not known; wires that end beside it: _74148_1_p10, _74148_1_p11, _74148_1_p12, 1'b0, 1'b0, 1'b0, CLK_t, 1'b1, _74174_2_p9, _74174_2_p10, _74174_2_p11
  // _74240 _74240: pin names not known; wires that end beside it: _74148_1_p10, _74148_1_p11, _74148_1_p12, 1'b0, 1'b0, 1'b0, 1'b0, 1'b0, INTO, INTO, BUS[0], BUS[1], BUS[2], BUS[3], BUS[4], BUS[5], BUS[6], BUS[7]
  nor nor_14 (nor_14_out, xor_1_out, xor_2_out, xor_3_out);
  xor xor_3 (xor_3_out, _74148_1_p12, _74174_2_p11);
  not not_6 (not_6_out, _74138_p11);
  // _74174 _74174_3: pin names not known; wires that end beside it: BUS[0], BUS[1], BUS[2], BUS[3], BUS[4], BUS[5], not_6_out, 1'b1, _74174_3_p9, _74174_3_p10
  // _74138 _74138: pin names not known; wires that end beside it: P[0], P[1], P[2], PCLK, PG5, 1'b0, _74138_p7, _74138_p8, _74138_p9, _74138_p10, _74138_p11
  and and_4 (ULK, INT_6, INT_7);
  Button #(.activeLow("true")) _2 (.out(INT_2));
  Button #(.activeLow("true")) _4 (.out(INT_4));
  Button #(.activeLow("true")) _5 (.out(INT_5));
  Button #(.activeLow("true")) _6 (.out(INT_6));
  Button #(.activeLow("true")) _7 (.out(INT_7));
  not not_7 (not_7_out, BUS[5]);
  not not_8 (not_8_out, BUS[6]);
  not not_9 (not_9_out, BUS[7]);
  not not_10 (not_10_out, _74138_p7);
  // _74574 _74574: pin names not known; wires that end beside it: BUS[0], BUS[1], BUS[2], BUS[3], BUS[4], BUS[5], BUS[6], BUS[7], _74174_3_p9, not_10_out, _74574_p11[0], _74574_p11[1], _74574_p11[2], _74574_p11[3], _74574_p11[4], _74574_p11[5], _74574_p11[6], _74574_p11[7]
  // _74244 _74244: pin names not known; wires that end beside it: _74574_p11[0], _74574_p11[1], _74574_p11[2], _74574_p11[3], _74574_p11[4], _74574_p11[5], _74574_p11[6], _74574_p11[7], IO0O, IO0O, BUS[0], BUS[1], BUS[2], BUS[3], BUS[4], BUS[5], BUS[6], BUS[7]
  // _74574 _74574_2: pin names not known; wires that end beside it: BUS[0], BUS[1], BUS[2], BUS[3], BUS[4], BUS[5], BUS[6], BUS[7], CRO, _74138_p9, BUS[0], BUS[1], BUS[2], BUS[3], BUS[4], BUS[5], BUS[6], BUS[7]
  // _74574 _74574_3: pin names not known; wires that end beside it: BUS[0], BUS[1], BUS[2], BUS[3], BUS[4], BUS[5], BUS[6], BUS[7], DRO, _74138_p10, BUS[0], BUS[1], BUS[2], BUS[3], BUS[4], BUS[5], BUS[6], BUS[7]
  or or_7 (or_7_out, nJC, not_7_out);
  or or_8 (or_8_out, nJNC, BUS[5]);
  or or_9 (or_9_out, nJZ, not_8_out);
  or or_10 (or_10_out, nJNZ, BUS[6]);
  or or_11 (or_11_out, nJV, not_9_out);
  or or_12 (or_12_out, nJNV, BUS[7]);
  nor nor_15 (nor_15_out, CIR0, CIR1, CIR3);
  not not_11 (not_11_out, _74138_p8);
  nand nand_5 (nand_5_out, or_7_out, or_8_out, or_9_out, or_10_out, or_11_out, or_12_out, nJMP_I, nor_15_out);
  // _74574 _74574_4: pin names not known; wires that end beside it: BUS[0], BUS[1], BUS[2], BUS[3], BUS[4], BUS[5], BUS[6], BUS[7], _74174_3_p10, not_11_out, _74574_4_p11[0], _74574_4_p11[1], _74574_4_p11[2], _74574_4_p11[3], _74574_4_p11[4], _74574_4_p11[5], _74574_4_p11[6], _74574_4_p11[7]
  // _74244 _74244_2: pin names not known; wires that end beside it: _74574_4_p11[0], _74574_4_p11[1], _74574_4_p11[2], _74574_4_p11[3], _74574_4_p11[4], _74574_4_p11[5], _74574_4_p11[6], _74574_4_p11[7], IO1O, IO1O, BUS[0], BUS[1], BUS[2], BUS[3], BUS[4], BUS[5], BUS[6], BUS[7]
  LedMatrix #(.ledPersistence("true"), .colAddrBits(5)) ledmatrix_1 (.rows(_74574_p11), .column(_74574_4_p11[4:0]));
  not not_12 (nJMP, nand_5_out);
  // _74574 _74574_5: pin names not known; wires that end beside it: BUS[0], BUS[1], BUS[2], BUS[3], BUS[4], BUS[5], BUS[6], BUS[7], nPCO, PCLLD, _74574_5_p11[0], _74574_5_p11[1], _74574_5_p11[2], _74574_5_p11[3], _74574_5_p11[4], _74574_5_p11[5], _74574_5_p11[6], _74574_5_p11[7]
  // _74574 _74574_6: pin names not known; wires that end beside it: AD[0], AD[1], AD[2], AD[3], AD[4], AD[5], AD[6], AD[7], nBCO_0, BCK_0, _74574_5_p11[0], _74574_5_p11[1], _74574_5_p11[2], _74574_5_p11[3], _74574_5_p11[4], _74574_5_p11[5], _74574_5_p11[6], _74574_5_p11[7]
  // _74574 _74574_7: pin names not known; wires that end beside it: AD[8], AD[9], AD[10], AD[11], AD[12], AD[13], AD[14], AD[15], nBCO_1, CIR0, _74574_7_p11[0], _74574_7_p11[1], _74574_7_p11[2], _74574_7_p11[3], _74574_7_p11[4], _74574_7_p11[5], _74574_7_p11[6], _74574_7_p11[7]
  // _74574 _74574_8: pin names not known; wires that end beside it: BUS[0], BUS[1], BUS[2], BUS[3], BUS[4], BUS[5], BUS[6], BUS[7], nPCO, PCMLD, _74574_7_p11[0], _74574_7_p11[1], _74574_7_p11[2], _74574_7_p11[3], _74574_7_p11[4], _74574_7_p11[5], _74574_7_p11[6], _74574_7_p11[7]
  // _74574 _74574_9: pin names not known; wires that end beside it: AD[8], AD[9], AD[10], AD[11], AD[12], AD[13], AD[14], AD[15], nBCO_0, BCK_0, _74574_7_p11[0], _74574_7_p11[1], _74574_7_p11[2], _74574_7_p11[3], _74574_7_p11[4], _74574_7_p11[5], _74574_7_p11[6], _74574_7_p11[7]
  // _74574 _74574_10: pin names not known; wires that end beside it: _74574_10_p1[16], _74574_10_p1[17], _74574_10_p1[18], _74574_10_p1[19], _74574_10_p1[20], _74574_10_p1[21], _74574_10_p1[22], _74574_10_p8[7], nBCO_1, CIR0, _74574_10_p11[0], _74574_10_p11[1], _74574_10_p11[2], _74574_10_p11[3], _74574_10_p11[4], _74574_10_p11[5], _74574_10_p11[6], _74574_10_p11[7]
  // _74574 _74574_11: pin names not known; wires that end beside it: BUS[0], BUS[1], BUS[2], BUS[3], BUS[4], BUS[5], BUS[6], BUS[7], nPCO, PCHLD, _74574_10_p11[0], _74574_10_p11[1], _74574_10_p11[2], _74574_10_p11[3], _74574_10_p11[4], _74574_10_p11[5], _74574_10_p11[6], _74574_10_p11[7]
  // _74574 _74574_12: pin names not known; wires that end beside it: _74574_10_p1[16], _74574_10_p1[17], _74574_10_p1[18], _74574_10_p1[19], _74574_10_p1[20], _74574_10_p1[21], _74574_10_p1[22], _74574_10_p8[7], nBCO_0, BCK_0, _74574_10_p11[0], _74574_10_p11[1], _74574_10_p11[2], _74574_10_p11[3], _74574_10_p11[4], _74574_10_p11[5], _74574_10_p11[6], _74574_10_p11[7]
  // _74161 _74161: pin names not known; wires that end beside it: _74574_5_p11[0], _74574_5_p11[1], _74574_5_p11[2], _74574_5_p11[3], nJMP, nINT, CLK_t, CKE, CKE, AD[0], AD[1], AD[2], AD[3], _74161_p14
  // _74161 _74161_2: pin names not known; wires that end beside it: _74574_5_p11[4], _74574_5_p11[5], _74574_5_p11[6], _74574_5_p11[7], nJMP, nINT, CLK_t, _74161_p14, _74161_p14, AD[4], AD[5], AD[6], AD[7], _74161_2_p14
  // _74574 _74161_3: pin names not known; wires that end beside it: AD[0], AD[1], AD[2], AD[3], AD[4], AD[5], AD[6], AD[7], nBCO_1, CIR0, _74574_5_p11[0], _74574_5_p11[1], _74574_5_p11[2], _74574_5_p11[3], _74574_5_p11[4], _74574_5_p11[5], _74574_5_p11[6], _74574_5_p11[7]
  // _74161 _74161_4: pin names not known; wires that end beside it: _74574_7_p11[0], _74574_7_p11[1], _74574_7_p11[2], _74574_7_p11[3], nJMP, nINT, CLK_t, _74161_2_p14, _74161_2_p14, AD[8], AD[9], AD[10], AD[11], _74161_4_p14
  // _74161 _74161_5: pin names not known; wires that end beside it: _74574_7_p11[4], _74574_7_p11[5], _74574_7_p11[6], _74574_7_p11[7], nJMP, nINT, CLK_t, _74161_4_p14, _74161_4_p14, AD[12], AD[13], AD[14], AD[15], _74161_5_p14
  // _74161 _74161_6: pin names not known; wires that end beside it: _74574_10_p11[0], _74574_10_p11[1], _74574_10_p11[2], _74574_10_p11[3], nJMP, nINT, CLK_t, _74161_5_p14, _74161_5_p14, _74574_10_p1[16], _74574_10_p1[17], _74574_10_p1[18], _74574_10_p1[19], _74161_6_p14
  // _74161 _74161_7: pin names not known; wires that end beside it: _74574_10_p11[4], _74574_10_p11[5], _74574_10_p11[6], _74574_10_p11[7], nJMP, nINT, CLK_t, _74161_6_p14, _74161_6_p14, _74574_10_p1[20], _74574_10_p1[21], _74574_10_p1[22], _74574_10_p8[7]
  not not_13 (not_13_out, PCLK);
  // _74244 _74244_3: pin names not known; wires that end beside it: _74574_5_p11[0], _74574_5_p11[1], _74574_5_p11[2], _74574_5_p11[3], _74574_5_p11[4], _74574_5_p11[5], _74574_5_p11[6], _74574_5_p11[7], PCLO, PCLO, BUS[0], BUS[1], BUS[2], BUS[3], BUS[4], BUS[5], BUS[6], BUS[7]
  // _74244 _74244_4: pin names not known; wires that end beside it: _74574_7_p11[0], _74574_7_p11[1], _74574_7_p11[2], _74574_7_p11[3], _74574_7_p11[4], _74574_7_p11[5], _74574_7_p11[6], _74574_7_p11[7], PCMO, PCMO, BUS[0], BUS[1], BUS[2], BUS[3], BUS[4], BUS[5], BUS[6], BUS[7]
  // _74244 _74244_5: pin names not known; wires that end beside it: _74574_10_p11[0], _74574_10_p11[1], _74574_10_p11[2], _74574_10_p11[3], _74574_10_p11[4], _74574_10_p11[5], _74574_10_p11[6], _74574_10_p11[7], PCHO, PCHO, BUS[0], BUS[1], BUS[2], BUS[3], BUS[4], BUS[5], BUS[6], BUS[7]
  // _74138 _74138_2: pin names not known; wires that end beside it: PS[0], PS[1], PS[2], 1'b1, 1'b0, 1'b0, PG2, PG3, PG4, PG5
  // _74138 _74138_3: pin names not known; wires that end beside it: P[0], P[1], P[2], PCLK, PG2, 1'b0, _74138_3_p7, _74138_3_p8, _74138_3_p9, nFBK, RD, WT, nRET, GED
  // _74138 _74138_4: pin names not known; wires that end beside it: P[0], P[1], P[2], not_13_out, PG3, 1'b0, nJMP_I, nHLT, nJC, nJNC, nJZ, nJNZ, nJV, nJNV
  // _74138 _74138_5: pin names not known; wires that end beside it: P[0], P[1], P[2], PCLK, PG4, 1'b0, nT0LLD, nT0HLD, nT1LLD, nT1HLD, _74138_5_p11, _74138_5_p12, nINT_3, INT_1
  // _74138 _74138_6: pin names not known; wires that end beside it: O[0], O[1], O[2], OS[0], OS[1], OS[2], RDTO, INTO, CRO, DRO, IO0O, IO1O
  not not_14 (PCLLD, _74138_3_p7);
  not not_15 (PCMLD, _74138_3_p8);
  not not_16 (PCHLD, _74138_3_p9);
  not not_17 (CTC, _74138_5_p11);
  not not_18 (CTI, _74138_5_p12);
  not not_19 (not_19_out, OS[0]);
  // _74138 _74138_7: pin names not known; wires that end beside it: O[0], O[1], O[2], not_19_out, OS[1], OS[2], nBUSO, PCLO, PCMO, PCHO
  // _74138 _74244_6: pin names not known; wires that end beside it: O[0], O[1], O[2], OS[0], OS[1], OS[2], RDTO
  // _74574 _74574_13: pin names not known; wires that end beside it: DT[0], DT[1], DT[2], DT[3], DT[4], DT[5], D6, D7, RDTO, CIR2, BUS[0], BUS[1], BUS[2], BUS[3], BUS[4], BUS[5], BUS[6], BUS[7]
  D_FF_AS d_ff_as_10 (.Set(~1'b1), .D(BUS[0]), .C(CTC), .Clr(~_74161_13_p10), .Q(d_ff_as_10_q));  // open: nQ
  D_FF_AS d_ff_as_11 (.Set(~1'b1), .D(BUS[1]), .C(CTC), .Clr(~INT_5), .Q(d_ff_as_11_q));  // open: nQ
  PullUp pullup_1 (.out(pullup_1_out));
  Fuse #(.Blown("true")) fuse_1 (.A(AOW), .B(pullup_1_out));
  not not_20 (not_20_out, _74574_10_p8[7]);
  // _74574 _74574_14: pin names not known; wires that end beside it: BUS[0], BUS[1], BUS[2], BUS[3], BUS[4], BUS[5], BUS[6], BUS[7], DTO, CIR0, DT[0], DT[1], DT[2], DT[3], DT[4], DT[5], D6, D7
  // _74161 _74161_8: pin names not known; wires that end beside it: BUS[0], BUS[1], BUS[2], BUS[3], nT0LLD, 1'b1, CLK_t, d_ff_as_10_q, d_ff_as_10_q, _74161_8_p10
  // _74161 _74161_9: pin names not known; wires that end beside it: BUS[4], BUS[5], BUS[6], BUS[7], nT0LLD, 1'b1, CLK_t, _74161_8_p10, _74161_8_p10, _74161_9_p10
  // _74161 _74161_10: pin names not known; wires that end beside it: BUS[0], BUS[1], BUS[2], BUS[3], nT1LLD, 1'b1, CLK_t, d_ff_as_11_q, d_ff_as_11_q, _74161_10_p10
  // _74161 _74161_11: pin names not known; wires that end beside it: BUS[4], BUS[5], BUS[6], BUS[7], nT1LLD, 1'b1, CLK_t, _74161_10_p10, _74161_10_p10, _74161_11_p10
  EEPROM #(.AddrBits(15), .isProgramMemory("true"), .Bits(8)) eeprom_1 (
    .A(AD[14:0]), .CS(~_74574_10_p8[7]), .WE(~pullup_1_out), .OE(~RAMO), .D({D7, D6, DT}));
  RAMSinglePortSel #(.AddrBits(23), .Bits(8)) ramsingleportsel_1 (
    .A({_74574_10_p1, AD}), .CS(~not_20_out), .WE(~AOW), .OE(~RAMO), .D({D7, D6, DT}));
  // _74174 _74174_4: pin names not known; wires that end beside it: DT[0], DT[1], DT[2], DT[3], DT[4], DT[5], PLD, 1'b1, P[0], P[1], P[2], PS[0], PS[1], PS[2]
  // _74174 _74174_5: pin names not known; wires that end beside it: DT[0], DT[1], DT[2], DT[3], DT[4], DT[5], OLD, 1'b1, O[0], O[1], O[2], OS[0], OS[1], OS[2]
  // _74574 _74574_15: pin names not known; wires that end beside it: DT[0], DT[1], DT[2], DT[3], DT[4], DT[5], D6, D7, nBUSO, BLD, BUS[0], BUS[1], BUS[2], BUS[3], BUS[4], BUS[5], BUS[6], BUS[7]
  // _74161 _74161_12: pin names not known; wires that end beside it: BUS[0], BUS[1], BUS[2], BUS[3], nT0HLD, 1'b1, CLK_t, _74161_9_p10, _74161_9_p10, _74161_12_p10
  // _74161 _74161_13: pin names not known; wires that end beside it: BUS[4], BUS[5], BUS[6], BUS[7], nT0HLD, 1'b1, CLK_t, _74161_12_p10, _74161_12_p10, _74161_13_p10
  // _74161 _74161_14: pin names not known; wires that end beside it: BUS[0], BUS[1], BUS[2], BUS[3], nT1HLD, 1'b1, CLK_t, _74161_11_p10, _74161_11_p10, _74161_14_p10
  // _74161 _74161_15: pin names not known; wires that end beside it: BUS[4], BUS[5], BUS[6], BUS[7], nT1HLD, 1'b1, CLK_t, _74161_14_p10, _74161_14_p10, _74161_15_p10
  and and_5 (INT_3, not_21_out, nINT_3);
  not not_21 (not_21_out, _74161_13_p10);
  not not_22 (INT_5, _74161_15_p10);
  // Probe on {PS, P}
  // Probe on {OS, O}
  // _74165 _74165_1: pin names not known; wires that end beside it: BUS[7], BUS[6], BUS[5], BUS[4], BUS[3], BUS[2], BUS[1], BUS[0], 1'b0, 1'b0, MCK, nMLD, _74165_1_p13, _74165_1_p14, _74165_1_p15, _74165_1_p16
  // _74273 _74273: pin names not known; wires that end beside it: BUS[0], BUS[1], BUS[2], BUS[3], BUS[4], BUS[5], BUS[6], BUS[7], ACLD, 1'b1, S[0], S[1], S[2], S[3], M, _74273_p16, MUL, DIV
  // _74138 _74138_8: pin names not known; wires that end beside it: P[0], P[1], P[2], PCLK, 1'b0, PG0, nACP, nAMR, nSTL, nSTR, nLDM, _74138_8_p12, _74138_8_p13
  not not_23 (not_23_out, nAOO);
  // _74138 _74138_9: pin names not known; wires that end beside it: PS[0], PS[1], PS[2], 1'b1, 1'b0, 1'b0, PG0, PG1
  // _74595 _74595_1: pin names not known; wires that end beside it: SO, not_23_out, 1'b1, SFK, nAOO, BUS[7], BUS[6], BUS[5], BUS[4], BUS[3], BUS[2], BUS[1], BUS[0], _74595_1_p14
  Reset reset_4 (.out(nRST));
  Button C (.out(C_out));
  LED led_7 (.in(CKE));
  // Probe on _74165_1_p15
  // Probe on _74165_1_p16
  LED led_8 (.in(_74273_p16));
  not not_24 (BLLD, _74138_8_p12);
  not not_25 (BHLD, _74138_8_p13);
  // Probe on _74595_1_p14
  Button K (.out(K_out));
  D_FF d_ff_1 (.D(d_ff_1_nq), .C(C_out), .Q(d_ff_1_q), .nQ(d_ff_1_nq));
  // _74574 _74574_16: pin names not known; wires that end beside it: BUS[0], BUS[1], BUS[2], BUS[3], BUS[4], BUS[5], BUS[6], BUS[7], _74165_1_p14, BHLD, _74574_16_p18[0], _74574_16_p18[1], _74574_16_p18[2], _74574_16_p18[3], _74574_16_p18[4], _74574_16_p18[5], _74574_16_p18[6], _74574_16_p18[7]
  nand nand_6 (nand_6_out, K_out, d_ff_1_q);
  nand nand_7 (nand_7_out, d_ff_1_nq, clk);
  LED led_9 (.in(PLD));
  D_FF_AS d_ff_as_12 (.Set(~nSTC), .D(Co), .C(~nREC), .Clr(~nCLC), .Q(Ci));  // open: nQ
  not not_26 (not_26_out, OS[0]);
  LED led_10 (.in(OLD));
  // _74138 _74138_10: pin names not known; wires that end beside it: P[0], P[1], P[2], PCLK, 1'b0, PG1, nAILD, nMLD, nSTC, nCLC, nREC, nNF, nCAI, _74138_10_p14
  // _74138 _74138_11: pin names not known; wires that end beside it: O[0], O[1], O[2], not_26_out, OS[1], OS[2], nUO, nDO, nAOO, nACO
  // _74595 _74595_2: pin names not known; wires that end beside it: Co, _74595_2_p2, 1'b1, DCK, nDO, BUS[0], BUS[1], BUS[2], BUS[3], BUS[4], BUS[5], BUS[6], BUS[7], _74595_2_p14
  not not_27 (_74595_2_p2, nDO);
  nand nand_8 (CLK_t, nand_6_out, nand_7_out);
  assign {nBH, nBL} = ~_74574_16_p18;  // Not not_28, 8 bits wide
  // _74244 _74244_7: pin names not known; wires that end beside it: S[0], S[1], S[2], S[3], M, Co, Z, OV, nACO, nACO, BUS[0], BUS[1], BUS[2], BUS[3], BUS[4], BUS[5], BUS[6], BUS[7]
  LED led_11 (.in(CLK_t));
  // _74574 _74574_17: pin names not known; wires that end beside it: BUS[0], BUS[1], BUS[2], BUS[3], BUS[4], BUS[5], BUS[6], BUS[7], _74165_1_p13, BLLD, _74574_16_p18[0], _74574_16_p18[1], _74574_16_p18[2], _74574_16_p18[3], _74574_16_p18[4], _74574_16_p18[5], _74574_16_p18[6], _74574_16_p18[7]
  not not_29 (ACLD, _74138_10_p14);
  // Probe on _74595_2_p14
  Seven_Seg_Hex seven_seg_hex_1 (.d({D7, D6, DT[5:4]}), .dp(1'b0));
  Seven_Seg_Hex seven_seg_hex_2 (.d(DT[3:0]), .dp(1'b0));
  // _74165 _74165_2: pin names not known; wires that end beside it: BUS[0], BUS[1], BUS[2], BUS[3], BUS[4], BUS[5], BUS[6], BUS[7], 1'b0, 1'b0, SFK, nAILD, SI, _74165_2_p14, _74165_2_p15
  and and_6 (and_6_out, nSTL, nSTR);
  nor nor_16 (nor_16_out, DIV, DCK, Co);
  Seven_Seg_Hex seven_seg_hex_3 (.d(AD[15:12]), .dp(1'b0));
  Seven_Seg_Hex seven_seg_hex_4 (.d(BUS[7:4]), .dp(1'b0));
  // Probe on _74165_2_p14
  // Probe on _74165_2_p15
  nand nand_9 (nand_9_out, nF7, nAH[3], ~nBH[3]);  // NAnd
  nand nand_10 (nand_10_out, ~nF7, ~nAH[3], nBH[3]);  // NAnd
  RS_FF_AS rs_ff_as_5 (.S(~nLDM), .R(~and_6_out), .Q(rs_ff_as_5_q));  // open: nQ
  RS_FF_AS rs_ff_as_6 (.S(~nSTR), .R(~nSTL), .Q(rs_ff_as_6_q), .nQ(rs_ff_as_6_nq));
  Seven_Seg_Hex seven_seg_hex_5 (.d(AD[11:8]), .dp(1'b0));
  Seven_Seg_Hex seven_seg_hex_6 (.d(BUS[3:0]), .dp(1'b0));
  nand nand_11 (OV, nand_9_out, 1'b1, nand_10_out);
  D_FF_AS d_ff_as_13 (.Set(~1'b1), .D(DCK), .C(~nACP), .Clr(~MUL), .Q(d_ff_as_13_q), .nQ(DCK));
  D_FF_AS d_ff_as_14 (.Set(~1'b1), .D(nor_16_out), .C(CLK_t), .Clr(~1'b1), .Q(d_ff_as_14_q));  // open: nQ
  Seven_Seg_Hex seven_seg_hex_7 (.d(not_30_out), .dp(1'b0));
  D_FF_AS d_ff_as_15 (.Set(~1'b1), .D(1'b1), .C(~SFK), .Clr(~nNF), .Q(d_ff_as_15_q));  // open: nQ
  Seven_Seg_Hex seven_seg_hex_8 (.d(AD[7:4]), .dp(1'b0));
  Seven_Seg_Hex seven_seg_hex_9 (.d({1'b0, OS}), .dp(1'b0));
  assign not_30_out = ~nAH;  // Not not_30, 4 bits wide
  or or_13 (S0, rs_ff_as_6_q, d_ff_as_13_q, rs_ff_as_5_q);
  or or_14 (S1, rs_ff_as_6_nq, d_ff_as_13_q, rs_ff_as_5_q);
  nor nor_17 (ACP, d_ff_as_14_q, nACP);
  nand nand_12 (SFK, DCK, nACP);
  nand nand_13 (MCK, SFK, d_ff_as_15_q);
  Seven_Seg_Hex seven_seg_hex_10 (.d(AD[3:0]), .dp(1'b0));
  Seven_Seg_Hex seven_seg_hex_11 (.d(not_31_out), .dp(1'b0));
  assign not_31_out = ~nAL;  // Not not_31, 4 bits wide
  Seven_Seg_Hex seven_seg_hex_12 (.d({1'b0, O}), .dp(1'b0));
  Seven_Seg_Hex seven_seg_hex_13 (.d(not_32_out), .dp(1'b0));
  assign not_32_out = ~nBH;  // Not not_32, 4 bits wide
  Seven_Seg_Hex seven_seg_hex_14 (.d({1'b0, PS}), .dp(1'b0));
  Seven_Seg_Hex seven_seg_hex_15 (.d(not_33_out), .dp(1'b0));
  Seven_Seg_Hex seven_seg_hex_16 (.d({1'b0, P}), .dp(1'b0));
  assign not_33_out = ~nBL;  // Not not_33, 4 bits wide
  D_FF_AS d_ff_as_16 (.Set(~1'b1), .D(Co), .C(SFK), .Clr(~nCAI), .Q(d_ff_as_16_q));  // open: nQ
  // _74181 _74181: pin names not known; wires that end beside it: nAL[0], nAL[1], nAL[2], nAL[3], nBL[0], nBL[1], nBL[2], nBL[3], S[0], S[1], S[2], S[3], _74181_p16[0], _74181_p16[1], _74181_p16[2], _74181_p16[3]
  // _74181 _74181_2: pin names not known; wires that end beside it: M, Ci, nAH[0], nAH[1], nAH[2], nAH[3], nBH[0], nBH[1], nBH[2], nBH[3], S[0], S[1], S[2], S[3], M, C_half, _74181_2_p17, C_half, _74181_2_p19[0], _74181_2_p19[1], _74181_2_p19[2], nF7, _74181_2_p23, Co
  // _74194 _74195: pin names not known; wires that end beside it: nAMR, S1, S0, ACP, d_ff_as_16_q, _74195_p6[3], BUS[7], _74195_p8[3], BUS[6], _74195_p8[2], BUS[5], _74195_p8[1], BUS[4], _74195_p8[0], nAMR, S1, S0
  assign nAH = ~_74195_p8;  // Not not_34, 4 bits wide
  assign not_35_out = ~{nF7, _74181_2_p19, _74181_p16};  // Not not_35, 8 bits wide
  // Probe on not_35_out
  and and_7 (Z, _74181_2_p17, _74181_2_p23);
  // _74540 _74540_1: pin names not known; wires that end beside it: _74181_p16[0], _74181_p16[1], _74181_p16[2], _74181_p16[3], _74181_2_p19[0], _74181_2_p19[1], _74181_2_p19[2], nF7, nUO, nUO, BUS[0], BUS[1], BUS[2], BUS[3], BUS[4], BUS[5], BUS[6], BUS[7]
  // _74194 _74195_2: pin names not known; wires that end beside it: ACP, _74195_p8[0], SI, BUS[3], _74195_p6[3], BUS[2], _74195_p6[2], BUS[1], _74195_p6[1], BUS[0], SO
  assign nAL = ~{_74195_p6, SO};  // Not not_36, 4 bits wide
  nand nand_14 (nand_14_out, VB, VB);
  nand nand_15 (nand_15_out, HR, HR);
  D_FF_AS #(.Default(1)) d_ff_as_17 (.Set(~1'b1), .D(1'b1), .C(nLX), .Clr(~nLXB), .Q(d_ff_as_17_q));  // open: nQ
  D_FF_AS #(.Default(1)) d_ff_as_18 (.Set(~nLX), .D(1'b0), .C(nLXB), .Clr(~1'b1), .Q(d_ff_as_18_q));  // open: nQ
  D_FF_AS #(.Default(1)) d_ff_as_19 (.Set(~1'b1), .D(1'b1), .C(nLY), .Clr(~nLYB), .Q(d_ff_as_19_q));  // open: nQ
  D_FF_AS #(.Default(1)) d_ff_as_20 (.Set(~nLY), .D(1'b0), .C(nLYB), .Clr(~1'b1), .Q(d_ff_as_20_q));  // open: nQ
  nor nor_18 (nor_18_out, CPV, VB);
  nor nor_19 (nor_19_out, CPV, nand_14_out);
  nor nor_20 (nor_20_out, CPH, HR);
  nor nor_21 (nor_21_out, CPH, nand_15_out);
  nor nor_22 (VCPE, nor_18_out, nor_23_out);
  nor nor_23 (nor_23_out, VCPE, nor_19_out);
  nor nor_24 (HCPE, nor_20_out, nor_25_out);
  nor nor_25 (nor_25_out, HCPE, nor_21_out);
  and and_8 (and_8_out, d_ff_as_18_q, nWVGA);
  and and_9 (and_9_out, d_ff_as_20_q, nWVGA);
  nand nand_16 (nVR, CPV, nor_23_out);
  nand nand_17 (nHR, CPH, nor_25_out);
  // _74273 _74273_2: pin names not known; wires that end beside it: BUS[0], BUS[1], BUS[2], BUS[3], BUS[4], BUS[5], BUS[6], BUS[7], nYP, 1'b1, _74273_2_p14[0], _74273_2_p14[1], _74273_2_p14[2], _74273_2_p14[3], _74273_2_p18[0], _74273_2_p18[1], _74273_2_p18[2], _74273_2_p18[3]
  // _74161 _74161_16: pin names not known; wires that end beside it: BUS[0], BUS[1], BUS[2], BUS[3], d_ff_as_17_q, 1'b1, and_8_out, d_ff_as_18_q, d_ff_as_18_q, _74161_16_p10[0], _74161_16_p10[1], _74161_16_p10[2], _74161_16_p10[3], _74161_16_p14
  // _74161 _74161_17: pin names not known; wires that end beside it: BUS[4], BUS[5], BUS[6], BUS[7], d_ff_as_17_q, 1'b1, and_8_out, _74161_16_p14, _74161_16_p14, _74161_17_p10[0], _74161_17_p10[1], _74161_17_p10[2], _74161_17_p10[3], _74161_17_p14
  // _74161 _74161_18: pin names not known; wires that end beside it: BUS[0], BUS[1], BUS[2], BUS[3], d_ff_as_19_q, 1'b1, and_9_out, _74161_17_p14, _74161_17_p14, _74161_18_p10[0], _74161_18_p10[1], _74161_18_p10[2], _74161_18_p10[3], _74161_18_p14
  // _74161 _74161_19: pin names not known; wires that end beside it: BUS[4], BUS[5], BUS[6], BUS[7], d_ff_as_19_q, 1'b1, and_9_out, _74161_18_p14, _74161_18_p14, _74161_19_p10[0], _74161_19_p10[1], _74161_19_p10[2], _74161_19_p10[3]
  nand nand_18 (CPV, nHR, nHR);
  not not_37 (nSEL, SEL);
  // _74283 _74283_1: pin names not known; wires that end beside it: _74273_2_p14[0], _74273_2_p14[1], _74273_2_p14[2], _74273_2_p14[3], YAD[0], YAD[1], YAD[2], YAD[3], 1'b0, _74283_1_p13[0], _74283_1_p13[1], _74283_1_p13[2], _74283_1_p13[3], _74283_1_p14
  // _74283 _74283_2: pin names not known; wires that end beside it: _74273_2_p18[0], _74273_2_p18[1], _74273_2_p18[2], _74273_2_p18[3], YAD[4], YAD[5], YAD[6], YAD[7], _74283_1_p14, _74283_2_p11[0], _74283_2_p11[1], _74283_2_p11[2], _74283_2_p11[3]
  // _74157 _74157_1: pin names not known; wires that end beside it: _74161_16_p10[0], _74161_16_p10[1], _74161_16_p10[2], _74161_16_p10[3], XAD[0], XAD[1], XAD[2], XAD[3], nSEL, 1'b0, _74157_1_p11[0], _74157_1_p11[1], _74157_1_p11[2], _74157_1_p11[3]
  // _74157 _74157_2: pin names not known; wires that end beside it: _74161_17_p10[0], _74161_17_p10[1], _74161_17_p10[2], _74161_17_p10[3], XAD[4], XAD[5], XAD[6], XAD[7], nSEL, 1'b0, _74157_2_p11[0], _74157_2_p11[1], _74157_2_p11[2], _74157_2_p11[3]
  // _74157 _74157_3: pin names not known; wires that end beside it: _74161_18_p10[0], _74161_18_p10[1], _74161_18_p10[2], _74161_18_p10[3], _74283_1_p13[0], _74283_1_p13[1], _74283_1_p13[2], _74283_1_p13[3], nSEL, 1'b0, _74157_3_p11[0], _74157_3_p11[1], _74157_3_p11[2], _74157_3_p11[3]
  // _74157 _74157_4: pin names not known; wires that end beside it: _74161_19_p10[0], _74161_19_p10[1], _74161_19_p10[2], _74161_19_p10[3], _74283_2_p11[0], _74283_2_p11[1], _74283_2_p11[2], _74283_2_p11[3], nSEL, 1'b0, _74157_4_p11[0], _74157_4_p11[1], _74157_4_p11[2], _74157_4_p11[3]
  // _74157 _74157_5: pin names not known; wires that end beside it: _74161_16_p10[0], _74161_16_p10[1], _74161_16_p10[2], _74161_16_p10[3], XAD[0], XAD[1], XAD[2], XAD[3], SEL, 1'b0, _74157_5_p11[0], _74157_5_p11[1], _74157_5_p11[2], _74157_5_p11[3]
  // _74157 _74157_6: pin names not known; wires that end beside it: _74161_17_p10[0], _74161_17_p10[1], _74161_17_p10[2], _74161_17_p10[3], XAD[4], XAD[5], XAD[6], XAD[7], SEL, 1'b0, _74157_6_p11[0], _74157_6_p11[1], _74157_6_p11[2], _74157_6_p11[3]
  // _74157 _74157_7: pin names not known; wires that end beside it: _74161_18_p10[0], _74161_18_p10[1], _74161_18_p10[2], _74161_18_p10[3], _74283_1_p13[0], _74283_1_p13[1], _74283_1_p13[2], _74283_1_p13[3], SEL, 1'b0, _74157_7_p11[0], _74157_7_p11[1], _74157_7_p11[2], _74157_7_p11[3]
  // _74157 _74157_8: pin names not known; wires that end beside it: _74161_19_p10[0], _74161_19_p10[1], _74161_19_p10[2], _74161_19_p10[3], _74283_2_p11[0], _74283_2_p11[1], _74283_2_p11[2], _74283_2_p11[3], SEL, 1'b0, _74157_8_p11[0], _74157_8_p11[1], _74157_8_p11[2], _74157_8_p11[3]
  // _74161 _74161_20: pin names not known; wires that end beside it: 1'b0, 1'b0, 1'b0, 1'b0, 1'b1, nVR, CPV, VCPE, VCPE, _74161_20_p10[0], YAD[0], YAD[1], YAD[2], _74161_20_p14
  // _74161 _74161_21: pin names not known; wires that end beside it: 1'b0, 1'b0, 1'b0, 1'b0, 1'b1, nVR, CPV, _74161_20_p14, _74161_20_p14, YAD[3], YAD[4], YAD[5], YAD[6], _74161_21_p14
  // _74161 _74161_22: pin names not known; wires that end beside it: 1'b0, 1'b0, 1'b0, 1'b0, 1'b1, nVR, CPV, _74161_21_p14, _74161_21_p14, YAD[7], YO, _74161_22_p12[2], _74161_22_p12[3]
  and and_10 (and_10_out, CPH, in_1);
  VGA vga_1 (.R(RO), .G(GO), .B({BO, 1'b0}), .H(HSY), .V(VSY), .C(and_10_out));
  and and_11 (CPH, in_1, clk_2);
  // _74244 _74244_8: pin names not known; wires that end beside it: BUS[0], BUS[1], BUS[2], BUS[3], BUS[4], BUS[5], BUS[6], BUS[7], nSEL, nSEL, _74244_8_p11[0], _74244_8_p11[1], _74244_8_p11[2], _74244_8_p11[3], _74244_8_p11[4], _74244_8_p11[5], _74244_8_p11[6], _74244_8_p11[7]
  // _74244 _74244_9: pin names not known; wires that end beside it: BUS[0], BUS[1], BUS[2], BUS[3], BUS[4], BUS[5], BUS[6], BUS[7], SEL, SEL, _74244_9_p11[0], _74244_9_p11[1], _74244_9_p11[2], _74244_9_p11[3], _74244_9_p11[4], _74244_9_p11[5], _74244_9_p11[6], _74244_9_p11[7]
  // Probe on {YO, YAD, _74161_20_p10[0]}
  nor nor_26 (nor_26_out, XO, YO);
  // _74688 _74688_1: pin names not known; wires that end beside it: _74161_20_p10[0], YAD[0], YAD[1], YAD[2], YAD[3], YAD[4], YAD[5], YAD[6], 1'b0, 1'b1, 1'b0, 1'b1, 1'b0, 1'b1, 1'b1, 1'b1, YO, _74688_1_p18
  or or_15 (VF, _74688_1_p18, ~YAD[7]);  // Or
  // _74688 _74688_2: pin names not known; wires that end beside it: _74161_20_p10[0], YAD[0], YAD[1], YAD[2], YAD[3], YAD[4], YAD[5], YAD[6], 1'b0, 1'b0, 1'b1, 1'b1, 1'b0, 1'b1, 1'b1, 1'b1, YO, _74688_2_p18
  or or_16 (VS, _74688_2_p18, ~YAD[7]);  // Or
  // _74688 _74688_3: pin names not known; wires that end beside it: _74161_20_p10[0], YAD[0], YAD[1], YAD[2], YAD[3], YAD[4], YAD[5], YAD[6], 1'b0, 1'b0, 1'b1, 1'b1, 1'b0, 1'b0, 1'b0, 1'b0, YAD[7], _74688_3_p18
  or or_17 (VB, _74688_3_p18, ~YO);  // Or
  assign RO = nor_26_out ? R : 3'bz;  // Driver driver_1
  assign BO = nor_26_out ? B : 2'bz;  // Driver driver_2
  assign GO = nor_26_out ? G : 3'bz;  // Driver driver_3
  or or_18 (or_18_out, _74157_4_p11[3], SEL);
  or or_19 (or_19_out, ~_74157_4_p11[3], SEL);  // Or
  or or_20 (or_20_out, _74157_8_p11[3], ~SEL);  // Or
  nand nand_19 (nand_19_out, _74157_8_p11[3], SEL);
  not not_38 (not_38_out, _74157_4_p11[3]);
  not not_39 (not_39_out, _74157_8_p11[3]);
  // _74161 _74161_23: pin names not known; wires that end beside it: 1'b0, 1'b0, 1'b0, 1'b0, 1'b1, nHR, CPH, HCPE, HCPE, _74161_23_p10[0], XAD[0], XAD[1], XAD[2], _74161_23_p14
  // _74161 _74161_24: pin names not known; wires that end beside it: 1'b0, 1'b0, 1'b0, 1'b0, 1'b1, nHR, CPH, _74161_23_p14, _74161_23_p14, XAD[3], XAD[4], XAD[5], XAD[6], _74161_24_p14
  // _74161 _74161_25: pin names not known; wires that end beside it: 1'b0, 1'b0, 1'b0, 1'b0, 1'b1, nHR, CPH, _74161_24_p14, _74161_24_p14, XAD[7], XO, _74161_25_p12[2], _74161_25_p12[3]
  RAMSinglePortSel #(.AddrBits(15), .Bits(8)) ramsingleportsel_2 (
    .A({_74157_4_p11[2:0], _74157_3_p11, _74157_2_p11, _74157_1_p11}), .CS(~_74157_4_p11[3]), .WE(~WE0),
    .OE(~or_18_out), .D(_74244_8_p11));
  RAMSinglePortSel #(.AddrBits(15), .Bits(8)) ramsingleportsel_3 (
    .A({_74157_4_p11[2:0], _74157_3_p11, _74157_2_p11, _74157_1_p11}), .CS(~not_38_out), .WE(~WE0),
    .OE(~or_19_out), .D(_74244_8_p11));
  RAMSinglePortSel #(.AddrBits(15), .Bits(8)) ramsingleportsel_4 (
    .A({_74157_8_p11[2:0], _74157_7_p11, _74157_6_p11, _74157_5_p11}), .CS(~_74157_8_p11[3]), .WE(~WE1),
    .OE(~or_20_out), .D(_74244_9_p11));
  RAMSinglePortSel #(.AddrBits(15), .Bits(8)) ramsingleportsel_5 (
    .A({_74157_8_p11[2:0], _74157_7_p11, _74157_6_p11, _74157_5_p11}), .CS(~not_39_out), .WE(~WE1),
    .OE(~nand_19_out), .D(_74244_9_p11));
  nand nand_20 (nand_20_out, HS, HSY);
  nand nand_21 (HSY, nand_20_out, HB);
  nand nand_22 (nand_22_out, VF, VSY);
  nand nand_23 (VSY, nand_22_out, VS);
  or or_21 (WE1, nWVGA, SEL);
  or or_22 (WE0, nWVGA, ~SEL);  // Or
  D_FF_AS #(.Default(1)) d_ff_as_21 (
    .Set(~nSAM), .D(d_ff_as_21_nq), .C(nIVS), .Clr(~1'b1), .Q(SEL), .nQ(d_ff_as_21_nq));
  // Probe on _74244_8_p11
  // Probe on _74244_9_p11
  // Probe on {XO, XAD, _74161_23_p10[0]}
  not not_40 (not_40_out, PS[0]);
  nand nand_24 (nand_24_out, PS[1], PS[2]);
  // _74157 _74157_9: pin names not known; wires that end beside it: _74244_8_p11[0], _74244_8_p11[1], _74244_8_p11[2], _74244_8_p11[3], _74244_9_p11[0], _74244_9_p11[1], _74244_9_p11[2], _74244_9_p11[3], SEL, 1'b0, R[0], R[1], R[2], B[0]
  // _74157 _74157_10: pin names not known; wires that end beside it: _74244_8_p11[4], _74244_8_p11[5], _74244_8_p11[6], _74244_8_p11[7], _74244_9_p11[4], _74244_9_p11[5], _74244_9_p11[6], _74244_9_p11[7], SEL, 1'b0, B[1], G[0], G[1], G[2]
  nand nand_25 (nand_25_out, XAD[7], XO);
  // _74138 _74138_12: pin names not known; wires that end beside it: P[0], P[1], P[2], PCLK, not_40_out, nand_24_out, nSAM, nIVS, nWVGA, nYP, nLXB, nLX, nLYB, nLY
  // _74688 _74688_4: pin names not known; wires that end beside it: _74161_23_p10[0], XAD[0], XAD[1], XAD[2], XAD[3], XAD[4], XAD[5], XAD[6], 1'b0, 1'b0, 1'b0, 1'b0, 1'b1, 1'b0, 1'b1, 1'b0, XAD[7], _74688_4_p18
  or or_23 (HS, _74688_4_p18, ~XO);  // Or
  // _74688 _74688_5: pin names not known; wires that end beside it: _74161_23_p10[0], XAD[0], XAD[1], XAD[2], XAD[3], XAD[4], XAD[5], XAD[6], 1'b0, 1'b0, 1'b0, 1'b0, 1'b1, 1'b1, 1'b0, 1'b1, XAD[7], _74688_5_p18
  or or_24 (HB, _74688_5_p18, ~XO);  // Or
  // _74688 _74688_6: pin names not known; wires that end beside it: _74161_23_p10[0], XAD[0], XAD[1], XAD[2], XAD[3], XAD[4], XAD[5], XAD[6], 1'b1, 1'b1, 1'b1, 1'b1, 1'b1, 1'b0, 1'b0, 1'b0, nand_25_out, HR

  // Other names for the same wires on the sheet: DT[7:6] = {D7, D6}; ROMO = RAMO

  // Notes on the sheet:
  //   clk: Hz: 1000
  //   clk_2: Hz: 2147483647
  //   Program Control Center
  //   Interrupt & IO
  //   Program Counter & Rom & Ram
  //   contents of eeprom_1 (hex, n*v repeats v):
  //   0,c0,0,14,89,1,6,85,0,81,9,f,8b,10,10,18,80,40,6,41,10,17,48,a8,0,40,6,a,41,1,b,29,
  //   c0,c0,86,30,10,44,1c,c0,10,10,18,0,0,0,0,0,0,41,1,c0,10,10,18,0,0,0,0,0,0,0,0,0,1,
  //   ff,4,4,4,ff,80,0,70,c8,a8,90,40,0,7f,80,40,0,0,7f,80,40,0,60,90,90,60,0,0,80,40,0,
  //   f,70,80,70,80,60,1e,1,60,90,90,60,0,0,f8,20,10,0,0,7f,80,40,0,0,70,88,88,7f,80,40,
  //   0,bf
  //   Arithmetic Logic Unit
  //   VGA Display Unit
  //   MADE BY LEFT HAND 
  //   an open sourse 74 gate computer
  //   NON
  //   AMR 
  //   BHLD 0xff
  //   MLD
  //   STR 201
  //   CLD
  //   CLC
  //   CAI
  //   NF
  //   UO
  //   ACP
  //   ACP
  //   ACP
  //   ACP
  //   ACP
  //   ACP
  //   ACP
  //   ACP
  //   ACP
  //   ACP
  //   ACP 
  //   ACP
  //   ACP 
  //   ACP
  //   ACP
  //   ACP
  //   CAI
  //   AOO
endmodule
